// Logisim project ALU 16 Bit.circ as structural Verilog: 14 circuits, main circuit Full Adder
module Full_Adder (
  input  A,
  input  B,
  input  Cin,
  output Sum,
  output Cout
);

  wire and_1_out, and_2_out, xor_1_out;

  xor xor_1 (xor_1_out, A, B);
  and and_1 (and_1_out, Cin, xor_1_out);
  and and_2 (and_2_out, B, A);
  xor xor_2 (Sum, xor_1_out, Cin);
  or or_1 (Cout, and_1_out, and_2_out);
endmodule

module Adder___Subtractor (
  input  B15,
  input  A15,
  input  B14,
  input  A14,
  input  B13,
  input  A13,
  input  B12,
  input  A12,
  input  B11,
  input  A11,
  input  B10,
  input  A10,
  input  B9,
  input  A9,
  input  B8,
  input  A8,
  input  B7,
  input  A7,
  input  B6,
  input  A6,
  input  B5,
  input  A5,
  input  B4,
  input  A4,
  input  B3,
  input  A3,
  input  B2,
  input  A2,
  input  B1,
  input  A1,
  input  B0,
  input  A0,
  input  M,
  output Over_Flow,
  output S15,
  output S14,
  output S13,
  output S12,
  output S11,
  output S10,
  output S9,
  output S8,
  output S7,
  output S6,
  output S5,
  output S4,
  output S3,
  output S2,
  output S1,
  output S0
);

  wire full_adder_2_cout, full_adder_3_cout, full_adder_4_cout, full_adder_5_cout, full_adder_6_cout,
       full_adder_7_cout, full_adder_8_cout, full_adder_9_cout, full_adder_10_cout, full_adder_11_cout,
       full_adder_12_cout, full_adder_13_cout, full_adder_14_cout, full_adder_15_cout, full_adder_16_cout,
       xor_1_out, xor_2_out, xor_3_out, xor_4_out, xor_5_out, xor_6_out, xor_7_out, xor_8_out, xor_9_out,
       xor_10_out, xor_11_out, xor_12_out, xor_13_out, xor_14_out, xor_15_out, xor_16_out;

  xor xor_1 (xor_1_out, M, B15);
  xor xor_2 (xor_2_out, M, B14);
  Full_Adder full_adder_1 (.A(A15), .B(xor_1_out), .Cin(full_adder_3_cout), .Sum(S15), .Cout(Over_Flow));
  xor xor_3 (xor_3_out, M, B13);
  Full_Adder full_adder_2 (.A(A13), .B(xor_3_out), .Cin(full_adder_4_cout), .Sum(S13), .Cout(full_adder_2_cout));
  Full_Adder full_adder_3 (.A(A14), .B(xor_2_out), .Cin(full_adder_2_cout), .Sum(S14), .Cout(full_adder_3_cout));
  xor xor_4 (xor_4_out, M, B12);
  Full_Adder full_adder_4 (.A(A12), .B(xor_4_out), .Cin(full_adder_5_cout), .Sum(S12), .Cout(full_adder_4_cout));
  xor xor_5 (xor_5_out, M, B11);
  Full_Adder full_adder_5 (.A(A11), .B(xor_5_out), .Cin(full_adder_6_cout), .Sum(S11), .Cout(full_adder_5_cout));
  xor xor_6 (xor_6_out, M, B10);
  Full_Adder full_adder_6 (.A(A10), .B(xor_6_out), .Cin(full_adder_7_cout), .Sum(S10), .Cout(full_adder_6_cout));
  xor xor_7 (xor_7_out, M, B9);
  Full_Adder full_adder_7 (.A(A9), .B(xor_7_out), .Cin(full_adder_8_cout), .Sum(S9), .Cout(full_adder_7_cout));
  xor xor_8 (xor_8_out, M, B7);
  xor xor_9 (xor_9_out, M, B8);
  Full_Adder full_adder_8 (.A(A8), .B(xor_9_out), .Cin(full_adder_9_cout), .Sum(S8), .Cout(full_adder_8_cout));
  xor xor_10 (xor_10_out, M, B6);
  Full_Adder full_adder_9 (.A(A7), .B(xor_8_out), .Cin(full_adder_10_cout), .Sum(S7), .Cout(full_adder_9_cout));
  xor xor_11 (xor_11_out, M, B5);
  Full_Adder full_adder_10 (.A(A6), .B(xor_10_out), .Cin(full_adder_11_cout), .Sum(S6), .Cout(full_adder_10_cout));
  Full_Adder full_adder_11 (.A(A5), .B(xor_11_out), .Cin(full_adder_12_cout), .Sum(S5), .Cout(full_adder_11_cout));
  xor xor_12 (xor_12_out, M, B4);
  Full_Adder full_adder_12 (.A(A4), .B(xor_12_out), .Cin(full_adder_13_cout), .Sum(S4), .Cout(full_adder_12_cout));
  xor xor_13 (xor_13_out, M, B3);
  Full_Adder full_adder_13 (.A(A3), .B(xor_13_out), .Cin(full_adder_14_cout), .Sum(S3), .Cout(full_adder_13_cout));
  xor xor_14 (xor_14_out, M, B2);
  Full_Adder full_adder_14 (.A(A2), .B(xor_14_out), .Cin(full_adder_15_cout), .Sum(S2), .Cout(full_adder_14_cout));
  xor xor_15 (xor_15_out, M, B1);
  Full_Adder full_adder_15 (.A(A1), .B(xor_15_out), .Cin(full_adder_16_cout), .Sum(S1), .Cout(full_adder_15_cout));
  xor xor_16 (xor_16_out, M, B0);
  Full_Adder full_adder_16 (.A(A0), .B(xor_16_out), .Cin(M), .Sum(S0), .Cout(full_adder_16_cout));
endmodule

module Multiplier_16Bit (
  input  A15,
  input  A14,
  input  A13,
  input  A12,
  input  A11,
  input  A10,
  input  A9,
  input  A8,
  input  A7,
  input  A6,
  input  A5,
  input  A4,
  input  A3,
  input  A2,
  input  A1,
  input  A0,
  input  A15_2,
  input  A14_2,
  input  A13_2,
  input  A12_2,
  input  A11_2,
  input  A10_2,
  input  A9_2,
  input  A8_2,
  input  A7_2,
  input  A6_2,
  input  A5_2,
  input  A4_2,
  input  A3_2,
  input  A2_2,
  input  A1_2,
  input  A0_2,
  output C31,
  output C30,
  output C29,
  output C28,
  output C27,
  output C26,
  output C25,
  output C24,
  output C23,
  output C22,
  output C21,
  output C20,
  output C19,
  output C18,
  output C17,
  output C16,
  output C15,
  output C14,
  output C13,
  output C12,
  output C11,
  output C10,
  output C9,
  output C8,
  output C7,
  output C6,
  output C5,
  output C4,
  output C3,
  output C2,
  output C1,
  output C0
);

  wire adder_subtractor_2_over_flow, adder_subtractor_2_s1, adder_subtractor_2_s2, adder_subtractor_2_s3,
       adder_subtractor_2_s4, adder_subtractor_2_s5, adder_subtractor_2_s6, adder_subtractor_2_s7,
       adder_subtractor_2_s8, adder_subtractor_2_s9, adder_subtractor_2_s10, adder_subtractor_2_s11,
       adder_subtractor_2_s12, adder_subtractor_2_s13, adder_subtractor_2_s14, adder_subtractor_2_s15,
       adder_subtractor_3_over_flow, adder_subtractor_3_s1, adder_subtractor_3_s2, adder_subtractor_3_s3,
       adder_subtractor_3_s4, adder_subtractor_3_s5, adder_subtractor_3_s6, adder_subtractor_3_s7,
       adder_subtractor_3_s8, adder_subtractor_3_s9, adder_subtractor_3_s10, adder_subtractor_3_s11,
       adder_subtractor_3_s12, adder_subtractor_3_s13, adder_subtractor_3_s14, adder_subtractor_3_s15,
       adder_subtractor_4_over_flow, adder_subtractor_4_s1, adder_subtractor_4_s2, adder_subtractor_4_s3,
       adder_subtractor_4_s4, adder_subtractor_4_s5, adder_subtractor_4_s6, adder_subtractor_4_s7,
       adder_subtractor_4_s8, adder_subtractor_4_s9, adder_subtractor_4_s10, adder_subtractor_4_s11,
       adder_subtractor_4_s12, adder_subtractor_4_s13, adder_subtractor_4_s14, adder_subtractor_4_s15,
       adder_subtractor_5_over_flow, adder_subtractor_5_s1, adder_subtractor_5_s2, adder_subtractor_5_s3,
       adder_subtractor_5_s4, adder_subtractor_5_s5, adder_subtractor_5_s6, adder_subtractor_5_s7,
       adder_subtractor_5_s8, adder_subtractor_5_s9, adder_subtractor_5_s10, adder_subtractor_5_s11,
       adder_subtractor_5_s12, adder_subtractor_5_s13, adder_subtractor_5_s14, adder_subtractor_5_s15,
       adder_subtractor_6_over_flow, adder_subtractor_6_s1, adder_subtractor_6_s2, adder_subtractor_6_s3,
       adder_subtractor_6_s4, adder_subtractor_6_s5, adder_subtractor_6_s6, adder_subtractor_6_s7,
       adder_subtractor_6_s8, adder_subtractor_6_s9, adder_subtractor_6_s10, adder_subtractor_6_s11,
       adder_subtractor_6_s12, adder_subtractor_6_s13, adder_subtractor_6_s14, adder_subtractor_6_s15,
       adder_subtractor_7_over_flow, adder_subtractor_7_s1, adder_subtractor_7_s2, adder_subtractor_7_s3,
       adder_subtractor_7_s4, adder_subtractor_7_s5, adder_subtractor_7_s6, adder_subtractor_7_s7,
       adder_subtractor_7_s8, adder_subtractor_7_s9, adder_subtractor_7_s10, adder_subtractor_7_s11,
       adder_subtractor_7_s12, adder_subtractor_7_s13, adder_subtractor_7_s14, adder_subtractor_7_s15,
       adder_subtractor_8_over_flow, adder_subtractor_8_s1, adder_subtractor_8_s2, adder_subtractor_8_s3,
       adder_subtractor_8_s4, adder_subtractor_8_s5, adder_subtractor_8_s6, adder_subtractor_8_s7,
       adder_subtractor_8_s8, adder_subtractor_8_s9, adder_subtractor_8_s10, adder_subtractor_8_s11,
       adder_subtractor_8_s12, adder_subtractor_8_s13, adder_subtractor_8_s14, adder_subtractor_8_s15,
       adder_subtractor_9_over_flow, adder_subtractor_9_s1, adder_subtractor_9_s2, adder_subtractor_9_s3,
       adder_subtractor_9_s4, adder_subtractor_9_s5, adder_subtractor_9_s6, adder_subtractor_9_s7,
       adder_subtractor_9_s8, adder_subtractor_9_s9, adder_subtractor_9_s10, adder_subtractor_9_s11,
       adder_subtractor_9_s12, adder_subtractor_9_s13, adder_subtractor_9_s14, adder_subtractor_9_s15,
       adder_subtractor_10_over_flow, adder_subtractor_10_s1, adder_subtractor_10_s2, adder_subtractor_10_s3,
       adder_subtractor_10_s4, adder_subtractor_10_s5, adder_subtractor_10_s6, adder_subtractor_10_s7,
       adder_subtractor_10_s8, adder_subtractor_10_s9, adder_subtractor_10_s10, adder_subtractor_10_s11,
       adder_subtractor_10_s12, adder_subtractor_10_s13, adder_subtractor_10_s14, adder_subtractor_10_s15,
       adder_subtractor_11_over_flow, adder_subtractor_11_s1, adder_subtractor_11_s2, adder_subtractor_11_s3,
       adder_subtractor_11_s4, adder_subtractor_11_s5, adder_subtractor_11_s6, adder_subtractor_11_s7,
       adder_subtractor_11_s8, adder_subtractor_11_s9, adder_subtractor_11_s10, adder_subtractor_11_s11,
       adder_subtractor_11_s12, adder_subtractor_11_s13, adder_subtractor_11_s14, adder_subtractor_11_s15,
       adder_subtractor_12_over_flow, adder_subtractor_12_s1, adder_subtractor_12_s2, adder_subtractor_12_s3,
       adder_subtractor_12_s4, adder_subtractor_12_s5, adder_subtractor_12_s6, adder_subtractor_12_s7,
       adder_subtractor_12_s8, adder_subtractor_12_s9, adder_subtractor_12_s10, adder_subtractor_12_s11,
       adder_subtractor_12_s12, adder_subtractor_12_s13, adder_subtractor_12_s14, adder_subtractor_12_s15,
       adder_subtractor_13_over_flow, adder_subtractor_13_s1, adder_subtractor_13_s2, adder_subtractor_13_s3,
       adder_subtractor_13_s4, adder_subtractor_13_s5, adder_subtractor_13_s6, adder_subtractor_13_s7,
       adder_subtractor_13_s8, adder_subtractor_13_s9, adder_subtractor_13_s10, adder_subtractor_13_s11,
       adder_subtractor_13_s12, adder_subtractor_13_s13, adder_subtractor_13_s14, adder_subtractor_13_s15,
       adder_subtractor_14_over_flow, adder_subtractor_14_s1, adder_subtractor_14_s2, adder_subtractor_14_s3,
       adder_subtractor_14_s4, adder_subtractor_14_s5, adder_subtractor_14_s6, adder_subtractor_14_s7,
       adder_subtractor_14_s8, adder_subtractor_14_s9, adder_subtractor_14_s10, adder_subtractor_14_s11,
       adder_subtractor_14_s12, adder_subtractor_14_s13, adder_subtractor_14_s14, adder_subtractor_14_s15,
       adder_subtractor_15_over_flow, adder_subtractor_15_s1, adder_subtractor_15_s2, adder_subtractor_15_s3,
       adder_subtractor_15_s4, adder_subtractor_15_s5, adder_subtractor_15_s6, adder_subtractor_15_s7,
       adder_subtractor_15_s8, adder_subtractor_15_s9, adder_subtractor_15_s10, adder_subtractor_15_s11,
       adder_subtractor_15_s12, adder_subtractor_15_s13, adder_subtractor_15_s14, adder_subtractor_15_s15,
       and_by_one_1_b0, and_by_one_1_b1, and_by_one_1_b2, and_by_one_1_b3, and_by_one_1_b4, and_by_one_1_b5,
       and_by_one_1_b6, and_by_one_1_b7, and_by_one_1_b8, and_by_one_1_b9, and_by_one_1_b10,
       and_by_one_1_b11, and_by_one_1_b12, and_by_one_1_b13, and_by_one_1_b14, and_by_one_1_b15,
       and_by_one_2_b0, and_by_one_2_b1, and_by_one_2_b2, and_by_one_2_b3, and_by_one_2_b4, and_by_one_2_b5,
       and_by_one_2_b6, and_by_one_2_b7, and_by_one_2_b8, and_by_one_2_b9, and_by_one_2_b10,
       and_by_one_2_b11, and_by_one_2_b12, and_by_one_2_b13, and_by_one_2_b14, and_by_one_2_b15,
       and_by_one_3_b0, and_by_one_3_b1, and_by_one_3_b2, and_by_one_3_b3, and_by_one_3_b4, and_by_one_3_b5,
       and_by_one_3_b6, and_by_one_3_b7, and_by_one_3_b8, and_by_one_3_b9, and_by_one_3_b10,
       and_by_one_3_b11, and_by_one_3_b12, and_by_one_3_b13, and_by_one_3_b14, and_by_one_3_b15,
       and_by_one_4_b0, and_by_one_4_b1, and_by_one_4_b2, and_by_one_4_b3, and_by_one_4_b4, and_by_one_4_b5,
       and_by_one_4_b6, and_by_one_4_b7, and_by_one_4_b8, and_by_one_4_b9, and_by_one_4_b10,
       and_by_one_4_b11, and_by_one_4_b12, and_by_one_4_b13, and_by_one_4_b14, and_by_one_4_b15,
       and_by_one_5_b0, and_by_one_5_b1, and_by_one_5_b2, and_by_one_5_b3, and_by_one_5_b4, and_by_one_5_b5,
       and_by_one_5_b6, and_by_one_5_b7, and_by_one_5_b8, and_by_one_5_b9, and_by_one_5_b10,
       and_by_one_5_b11, and_by_one_5_b12, and_by_one_5_b13, and_by_one_5_b14, and_by_one_5_b15,
       and_by_one_6_b0, and_by_one_6_b1, and_by_one_6_b2, and_by_one_6_b3, and_by_one_6_b4, and_by_one_6_b5,
       and_by_one_6_b6, and_by_one_6_b7, and_by_one_6_b8, and_by_one_6_b9, and_by_one_6_b10,
       and_by_one_6_b11, and_by_one_6_b12, and_by_one_6_b13, and_by_one_6_b14, and_by_one_6_b15,
       and_by_one_7_b0, and_by_one_7_b1, and_by_one_7_b2, and_by_one_7_b3, and_by_one_7_b4, and_by_one_7_b5,
       and_by_one_7_b6, and_by_one_7_b7, and_by_one_7_b8, and_by_one_7_b9, and_by_one_7_b10,
       and_by_one_7_b11, and_by_one_7_b12, and_by_one_7_b13, and_by_one_7_b14, and_by_one_7_b15,
       and_by_one_8_b0, and_by_one_8_b1, and_by_one_8_b2, and_by_one_8_b3, and_by_one_8_b4, and_by_one_8_b5,
       and_by_one_8_b6, and_by_one_8_b7, and_by_one_8_b8, and_by_one_8_b9, and_by_one_8_b10,
       and_by_one_8_b11, and_by_one_8_b12, and_by_one_8_b13, and_by_one_8_b14, and_by_one_8_b15,
       and_by_one_9_b0, and_by_one_9_b1, and_by_one_9_b2, and_by_one_9_b3, and_by_one_9_b4, and_by_one_9_b5,
       and_by_one_9_b6, and_by_one_9_b7, and_by_one_9_b8, and_by_one_9_b9, and_by_one_9_b10,
       and_by_one_9_b11, and_by_one_9_b12, and_by_one_9_b13, and_by_one_9_b14, and_by_one_9_b15,
       and_by_one_10_b0, and_by_one_10_b1, and_by_one_10_b2, and_by_one_10_b3, and_by_one_10_b4,
       and_by_one_10_b5, and_by_one_10_b6, and_by_one_10_b7, and_by_one_10_b8, and_by_one_10_b9,
       and_by_one_10_b10, and_by_one_10_b11, and_by_one_10_b12, and_by_one_10_b13, and_by_one_10_b14,
       and_by_one_10_b15, and_by_one_11_b0, and_by_one_11_b1, and_by_one_11_b2, and_by_one_11_b3,
       and_by_one_11_b4, and_by_one_11_b5, and_by_one_11_b6, and_by_one_11_b7, and_by_one_11_b8,
       and_by_one_11_b9, and_by_one_11_b10, and_by_one_11_b11, and_by_one_11_b12, and_by_one_11_b13,
       and_by_one_11_b14, and_by_one_11_b15, and_by_one_12_b0, and_by_one_12_b1, and_by_one_12_b2,
       and_by_one_12_b3, and_by_one_12_b4, and_by_one_12_b5, and_by_one_12_b6, and_by_one_12_b7,
       and_by_one_12_b8, and_by_one_12_b9, and_by_one_12_b10, and_by_one_12_b11, and_by_one_12_b12,
       and_by_one_12_b13, and_by_one_12_b14, and_by_one_12_b15, and_by_one_13_b0, and_by_one_13_b1,
       and_by_one_13_b2, and_by_one_13_b3, and_by_one_13_b4, and_by_one_13_b5, and_by_one_13_b6,
       and_by_one_13_b7, and_by_one_13_b8, and_by_one_13_b9, and_by_one_13_b10, and_by_one_13_b11,
       and_by_one_13_b12, and_by_one_13_b13, and_by_one_13_b14, and_by_one_13_b15, and_by_one_14_b0,
       and_by_one_14_b1, and_by_one_14_b2, and_by_one_14_b3, and_by_one_14_b4, and_by_one_14_b5,
       and_by_one_14_b6, and_by_one_14_b7, and_by_one_14_b8, and_by_one_14_b9, and_by_one_14_b10,
       and_by_one_14_b11, and_by_one_14_b12, and_by_one_14_b13, and_by_one_14_b14, and_by_one_14_b15,
       and_by_one_15_b0, and_by_one_15_b1, and_by_one_15_b2, and_by_one_15_b3, and_by_one_15_b4,
       and_by_one_15_b5, and_by_one_15_b6, and_by_one_15_b7, and_by_one_15_b8, and_by_one_15_b9,
       and_by_one_15_b10, and_by_one_15_b11, and_by_one_15_b12, and_by_one_15_b13, and_by_one_15_b14,
       and_by_one_15_b15, and_by_one_16_b1, and_by_one_16_b2, and_by_one_16_b3, and_by_one_16_b4,
       and_by_one_16_b5, and_by_one_16_b6, and_by_one_16_b7, and_by_one_16_b8, and_by_one_16_b9,
       and_by_one_16_b10, and_by_one_16_b11, and_by_one_16_b12, and_by_one_16_b13, and_by_one_16_b14,
       and_by_one_16_b15;

  And_By_one and_by_one_1 (
    .Input(A15_2), .A15(A15), .A14(A14), .A13(A13), .A12(A12), .A11(A11), .A10(A10), .A9(A9), .A8(A8),
    .A7(A7), .A6(A6), .A5(A5), .A4(A4), .A3(A3), .A2(A2), .A1(A1), .A0(A0), .B15(and_by_one_1_b15),
    .B14(and_by_one_1_b14), .B13(and_by_one_1_b13), .B12(and_by_one_1_b12), .B11(and_by_one_1_b11),
    .B10(and_by_one_1_b10), .B9(and_by_one_1_b9), .B8(and_by_one_1_b8), .B7(and_by_one_1_b7),
    .B6(and_by_one_1_b6), .B5(and_by_one_1_b5), .B4(and_by_one_1_b4), .B3(and_by_one_1_b3),
    .B2(and_by_one_1_b2), .B1(and_by_one_1_b1), .B0(and_by_one_1_b0));
  And_By_one and_by_one_2 (
    .Input(A14_2), .A15(A15), .A14(A14), .A13(A13), .A12(A12), .A11(A11), .A10(A10), .A9(A9), .A8(A8),
    .A7(A7), .A6(A6), .A5(A5), .A4(A4), .A3(A3), .A2(A2), .A1(A1), .A0(A0), .B15(and_by_one_2_b15),
    .B14(and_by_one_2_b14), .B13(and_by_one_2_b13), .B12(and_by_one_2_b12), .B11(and_by_one_2_b11),
    .B10(and_by_one_2_b10), .B9(and_by_one_2_b9), .B8(and_by_one_2_b8), .B7(and_by_one_2_b7),
    .B6(and_by_one_2_b6), .B5(and_by_one_2_b5), .B4(and_by_one_2_b4), .B3(and_by_one_2_b3),
    .B2(and_by_one_2_b2), .B1(and_by_one_2_b1), .B0(and_by_one_2_b0));
  And_By_one and_by_one_3 (
    .Input(A13_2), .A15(A15), .A14(A14), .A13(A13), .A12(A12), .A11(A11), .A10(A10), .A9(A9), .A8(A8),
    .A7(A7), .A6(A6), .A5(A5), .A4(A4), .A3(A3), .A2(A2), .A1(A1), .A0(A0), .B15(and_by_one_3_b15),
    .B14(and_by_one_3_b14), .B13(and_by_one_3_b13), .B12(and_by_one_3_b12), .B11(and_by_one_3_b11),
    .B10(and_by_one_3_b10), .B9(and_by_one_3_b9), .B8(and_by_one_3_b8), .B7(and_by_one_3_b7),
    .B6(and_by_one_3_b6), .B5(and_by_one_3_b5), .B4(and_by_one_3_b4), .B3(and_by_one_3_b3),
    .B2(and_by_one_3_b2), .B1(and_by_one_3_b1), .B0(and_by_one_3_b0));
  Adder___Subtractor adder_subtractor_1 (
    .M(1'b0), .B15(and_by_one_1_b15), .A15(adder_subtractor_2_over_flow), .B14(and_by_one_1_b14),
    .A14(adder_subtractor_2_s15), .B13(and_by_one_1_b13), .A13(adder_subtractor_2_s14),
    .B12(and_by_one_1_b12), .A12(adder_subtractor_2_s13), .B11(and_by_one_1_b11),
    .A11(adder_subtractor_2_s12), .B10(and_by_one_1_b10), .A10(adder_subtractor_2_s11), .B9(and_by_one_1_b9),
    .A9(adder_subtractor_2_s10), .B8(and_by_one_1_b8), .A8(adder_subtractor_2_s9), .B7(and_by_one_1_b7),
    .A7(adder_subtractor_2_s8), .B6(and_by_one_1_b6), .A6(adder_subtractor_2_s7), .B5(and_by_one_1_b5),
    .A5(adder_subtractor_2_s6), .B4(and_by_one_1_b4), .A4(adder_subtractor_2_s5), .B3(and_by_one_1_b3),
    .A3(adder_subtractor_2_s4), .B2(and_by_one_1_b2), .A2(adder_subtractor_2_s3), .B1(and_by_one_1_b1),
    .A1(adder_subtractor_2_s2), .B0(and_by_one_1_b0), .A0(adder_subtractor_2_s1), .Over_Flow(C31), .S15(C30),
    .S14(C29), .S13(C28), .S12(C27), .S11(C26), .S10(C25), .S9(C24), .S8(C23), .S7(C22), .S6(C21), .S5(C20),
    .S4(C19), .S3(C18), .S2(C17), .S1(C16), .S0(C15));
  And_By_one and_by_one_4 (
    .Input(A12_2), .A15(A15), .A14(A14), .A13(A13), .A12(A12), .A11(A11), .A10(A10), .A9(A9), .A8(A8),
    .A7(A7), .A6(A6), .A5(A5), .A4(A4), .A3(A3), .A2(A2), .A1(A1), .A0(A0), .B15(and_by_one_4_b15),
    .B14(and_by_one_4_b14), .B13(and_by_one_4_b13), .B12(and_by_one_4_b12), .B11(and_by_one_4_b11),
    .B10(and_by_one_4_b10), .B9(and_by_one_4_b9), .B8(and_by_one_4_b8), .B7(and_by_one_4_b7),
    .B6(and_by_one_4_b6), .B5(and_by_one_4_b5), .B4(and_by_one_4_b4), .B3(and_by_one_4_b3),
    .B2(and_by_one_4_b2), .B1(and_by_one_4_b1), .B0(and_by_one_4_b0));
  Adder___Subtractor adder_subtractor_2 (
    .M(1'b0), .B15(and_by_one_2_b15), .A15(adder_subtractor_3_over_flow), .B14(and_by_one_2_b14),
    .A14(adder_subtractor_3_s15), .B13(and_by_one_2_b13), .A13(adder_subtractor_3_s14),
    .B12(and_by_one_2_b12), .A12(adder_subtractor_3_s13), .B11(and_by_one_2_b11),
    .A11(adder_subtractor_3_s12), .B10(and_by_one_2_b10), .A10(adder_subtractor_3_s11), .B9(and_by_one_2_b9),
    .A9(adder_subtractor_3_s10), .B8(and_by_one_2_b8), .A8(adder_subtractor_3_s9), .B7(and_by_one_2_b7),
    .A7(adder_subtractor_3_s8), .B6(and_by_one_2_b6), .A6(adder_subtractor_3_s7), .B5(and_by_one_2_b5),
    .A5(adder_subtractor_3_s6), .B4(and_by_one_2_b4), .A4(adder_subtractor_3_s5), .B3(and_by_one_2_b3),
    .A3(adder_subtractor_3_s4), .B2(and_by_one_2_b2), .A2(adder_subtractor_3_s3), .B1(and_by_one_2_b1),
    .A1(adder_subtractor_3_s2), .B0(and_by_one_2_b0), .A0(adder_subtractor_3_s1),
    .Over_Flow(adder_subtractor_2_over_flow), .S15(adder_subtractor_2_s15), .S14(adder_subtractor_2_s14),
    .S13(adder_subtractor_2_s13), .S12(adder_subtractor_2_s12), .S11(adder_subtractor_2_s11),
    .S10(adder_subtractor_2_s10), .S9(adder_subtractor_2_s9), .S8(adder_subtractor_2_s8),
    .S7(adder_subtractor_2_s7), .S6(adder_subtractor_2_s6), .S5(adder_subtractor_2_s5),
    .S4(adder_subtractor_2_s4), .S3(adder_subtractor_2_s3), .S2(adder_subtractor_2_s2),
    .S1(adder_subtractor_2_s1), .S0(C14));
  And_By_one and_by_one_5 (
    .Input(A11_2), .A15(A15), .A14(A14), .A13(A13), .A12(A12), .A11(A11), .A10(A10), .A9(A9), .A8(A8),
    .A7(A7), .A6(A6), .A5(A5), .A4(A4), .A3(A3), .A2(A2), .A1(A1), .A0(A0), .B15(and_by_one_5_b15),
    .B14(and_by_one_5_b14), .B13(and_by_one_5_b13), .B12(and_by_one_5_b12), .B11(and_by_one_5_b11),
    .B10(and_by_one_5_b10), .B9(and_by_one_5_b9), .B8(and_by_one_5_b8), .B7(and_by_one_5_b7),
    .B6(and_by_one_5_b6), .B5(and_by_one_5_b5), .B4(and_by_one_5_b4), .B3(and_by_one_5_b3),
    .B2(and_by_one_5_b2), .B1(and_by_one_5_b1), .B0(and_by_one_5_b0));
  Adder___Subtractor adder_subtractor_3 (
    .M(1'b0), .B15(and_by_one_3_b15), .A15(adder_subtractor_4_over_flow), .B14(and_by_one_3_b14),
    .A14(adder_subtractor_4_s15), .B13(and_by_one_3_b13), .A13(adder_subtractor_4_s14),
    .B12(and_by_one_3_b12), .A12(adder_subtractor_4_s13), .B11(and_by_one_3_b11),
    .A11(adder_subtractor_4_s12), .B10(and_by_one_3_b10), .A10(adder_subtractor_4_s11), .B9(and_by_one_3_b9),
    .A9(adder_subtractor_4_s10), .B8(and_by_one_3_b8), .A8(adder_subtractor_4_s9), .B7(and_by_one_3_b7),
    .A7(adder_subtractor_4_s8), .B6(and_by_one_3_b6), .A6(adder_subtractor_4_s7), .B5(and_by_one_3_b5),
    .A5(adder_subtractor_4_s6), .B4(and_by_one_3_b4), .A4(adder_subtractor_4_s5), .B3(and_by_one_3_b3),
    .A3(adder_subtractor_4_s4), .B2(and_by_one_3_b2), .A2(adder_subtractor_4_s3), .B1(and_by_one_3_b1),
    .A1(adder_subtractor_4_s2), .B0(and_by_one_3_b0), .A0(adder_subtractor_4_s1),
    .Over_Flow(adder_subtractor_3_over_flow), .S15(adder_subtractor_3_s15), .S14(adder_subtractor_3_s14),
    .S13(adder_subtractor_3_s13), .S12(adder_subtractor_3_s12), .S11(adder_subtractor_3_s11),
    .S10(adder_subtractor_3_s10), .S9(adder_subtractor_3_s9), .S8(adder_subtractor_3_s8),
    .S7(adder_subtractor_3_s7), .S6(adder_subtractor_3_s6), .S5(adder_subtractor_3_s5),
    .S4(adder_subtractor_3_s4), .S3(adder_subtractor_3_s3), .S2(adder_subtractor_3_s2),
    .S1(adder_subtractor_3_s1), .S0(C13));
  And_By_one and_by_one_6 (
    .Input(A10_2), .A15(A15), .A14(A14), .A13(A13), .A12(A12), .A11(A11), .A10(A10), .A9(A9), .A8(A8),
    .A7(A7), .A6(A6), .A5(A5), .A4(A4), .A3(A3), .A2(A2), .A1(A1), .A0(A0), .B15(and_by_one_6_b15),
    .B14(and_by_one_6_b14), .B13(and_by_one_6_b13), .B12(and_by_one_6_b12), .B11(and_by_one_6_b11),
    .B10(and_by_one_6_b10), .B9(and_by_one_6_b9), .B8(and_by_one_6_b8), .B7(and_by_one_6_b7),
    .B6(and_by_one_6_b6), .B5(and_by_one_6_b5), .B4(and_by_one_6_b4), .B3(and_by_one_6_b3),
    .B2(and_by_one_6_b2), .B1(and_by_one_6_b1), .B0(and_by_one_6_b0));
  Adder___Subtractor adder_subtractor_4 (
    .M(1'b0), .B15(and_by_one_4_b15), .A15(adder_subtractor_5_over_flow), .B14(and_by_one_4_b14),
    .A14(adder_subtractor_5_s15), .B13(and_by_one_4_b13), .A13(adder_subtractor_5_s14),
    .B12(and_by_one_4_b12), .A12(adder_subtractor_5_s13), .B11(and_by_one_4_b11),
    .A11(adder_subtractor_5_s12), .B10(and_by_one_4_b10), .A10(adder_subtractor_5_s11), .B9(and_by_one_4_b9),
    .A9(adder_subtractor_5_s10), .B8(and_by_one_4_b8), .A8(adder_subtractor_5_s9), .B7(and_by_one_4_b7),
    .A7(adder_subtractor_5_s8), .B6(and_by_one_4_b6), .A6(adder_subtractor_5_s7), .B5(and_by_one_4_b5),
    .A5(adder_subtractor_5_s6), .B4(and_by_one_4_b4), .A4(adder_subtractor_5_s5), .B3(and_by_one_4_b3),
    .A3(adder_subtractor_5_s4), .B2(and_by_one_4_b2), .A2(adder_subtractor_5_s3), .B1(and_by_one_4_b1),
    .A1(adder_subtractor_5_s2), .B0(and_by_one_4_b0), .A0(adder_subtractor_5_s1),
    .Over_Flow(adder_subtractor_4_over_flow), .S15(adder_subtractor_4_s15), .S14(adder_subtractor_4_s14),
    .S13(adder_subtractor_4_s13), .S12(adder_subtractor_4_s12), .S11(adder_subtractor_4_s11),
    .S10(adder_subtractor_4_s10), .S9(adder_subtractor_4_s9), .S8(adder_subtractor_4_s8),
    .S7(adder_subtractor_4_s7), .S6(adder_subtractor_4_s6), .S5(adder_subtractor_4_s5),
    .S4(adder_subtractor_4_s4), .S3(adder_subtractor_4_s3), .S2(adder_subtractor_4_s2),
    .S1(adder_subtractor_4_s1), .S0(C12));
  And_By_one and_by_one_7 (
    .Input(A9_2), .A15(A15), .A14(A14), .A13(A13), .A12(A12), .A11(A11), .A10(A10), .A9(A9), .A8(A8),
    .A7(A7), .A6(A6), .A5(A5), .A4(A4), .A3(A3), .A2(A2), .A1(A1), .A0(A0), .B15(and_by_one_7_b15),
    .B14(and_by_one_7_b14), .B13(and_by_one_7_b13), .B12(and_by_one_7_b12), .B11(and_by_one_7_b11),
    .B10(and_by_one_7_b10), .B9(and_by_one_7_b9), .B8(and_by_one_7_b8), .B7(and_by_one_7_b7),
    .B6(and_by_one_7_b6), .B5(and_by_one_7_b5), .B4(and_by_one_7_b4), .B3(and_by_one_7_b3),
    .B2(and_by_one_7_b2), .B1(and_by_one_7_b1), .B0(and_by_one_7_b0));
  Adder___Subtractor adder_subtractor_5 (
    .M(1'b0), .B15(and_by_one_5_b15), .A15(adder_subtractor_6_over_flow), .B14(and_by_one_5_b14),
    .A14(adder_subtractor_6_s15), .B13(and_by_one_5_b13), .A13(adder_subtractor_6_s14),
    .B12(and_by_one_5_b12), .A12(adder_subtractor_6_s13), .B11(and_by_one_5_b11),
    .A11(adder_subtractor_6_s12), .B10(and_by_one_5_b10), .A10(adder_subtractor_6_s11), .B9(and_by_one_5_b9),
    .A9(adder_subtractor_6_s10), .B8(and_by_one_5_b8), .A8(adder_subtractor_6_s9), .B7(and_by_one_5_b7),
    .A7(adder_subtractor_6_s8), .B6(and_by_one_5_b6), .A6(adder_subtractor_6_s7), .B5(and_by_one_5_b5),
    .A5(adder_subtractor_6_s6), .B4(and_by_one_5_b4), .A4(adder_subtractor_6_s5), .B3(and_by_one_5_b3),
    .A3(adder_subtractor_6_s4), .B2(and_by_one_5_b2), .A2(adder_subtractor_6_s3), .B1(and_by_one_5_b1),
    .A1(adder_subtractor_6_s2), .B0(and_by_one_5_b0), .A0(adder_subtractor_6_s1),
    .Over_Flow(adder_subtractor_5_over_flow), .S15(adder_subtractor_5_s15), .S14(adder_subtractor_5_s14),
    .S13(adder_subtractor_5_s13), .S12(adder_subtractor_5_s12), .S11(adder_subtractor_5_s11),
    .S10(adder_subtractor_5_s10), .S9(adder_subtractor_5_s9), .S8(adder_subtractor_5_s8),
    .S7(adder_subtractor_5_s7), .S6(adder_subtractor_5_s6), .S5(adder_subtractor_5_s5),
    .S4(adder_subtractor_5_s4), .S3(adder_subtractor_5_s3), .S2(adder_subtractor_5_s2),
    .S1(adder_subtractor_5_s1), .S0(C11));
  And_By_one and_by_one_8 (
    .Input(A8_2), .A15(A15), .A14(A14), .A13(A13), .A12(A12), .A11(A11), .A10(A10), .A9(A9), .A8(A8),
    .A7(A7), .A6(A6), .A5(A5), .A4(A4), .A3(A3), .A2(A2), .A1(A1), .A0(A0), .B15(and_by_one_8_b15),
    .B14(and_by_one_8_b14), .B13(and_by_one_8_b13), .B12(and_by_one_8_b12), .B11(and_by_one_8_b11),
    .B10(and_by_one_8_b10), .B9(and_by_one_8_b9), .B8(and_by_one_8_b8), .B7(and_by_one_8_b7),
    .B6(and_by_one_8_b6), .B5(and_by_one_8_b5), .B4(and_by_one_8_b4), .B3(and_by_one_8_b3),
    .B2(and_by_one_8_b2), .B1(and_by_one_8_b1), .B0(and_by_one_8_b0));
  Adder___Subtractor adder_subtractor_6 (
    .M(1'b0), .B15(and_by_one_6_b15), .A15(adder_subtractor_7_over_flow), .B14(and_by_one_6_b14),
    .A14(adder_subtractor_7_s15), .B13(and_by_one_6_b13), .A13(adder_subtractor_7_s14),
    .B12(and_by_one_6_b12), .A12(adder_subtractor_7_s13), .B11(and_by_one_6_b11),
    .A11(adder_subtractor_7_s12), .B10(and_by_one_6_b10), .A10(adder_subtractor_7_s11), .B9(and_by_one_6_b9),
    .A9(adder_subtractor_7_s10), .B8(and_by_one_6_b8), .A8(adder_subtractor_7_s9), .B7(and_by_one_6_b7),
    .A7(adder_subtractor_7_s8), .B6(and_by_one_6_b6), .A6(adder_subtractor_7_s7), .B5(and_by_one_6_b5),
    .A5(adder_subtractor_7_s6), .B4(and_by_one_6_b4), .A4(adder_subtractor_7_s5), .B3(and_by_one_6_b3),
    .A3(adder_subtractor_7_s4), .B2(and_by_one_6_b2), .A2(adder_subtractor_7_s3), .B1(and_by_one_6_b1),
    .A1(adder_subtractor_7_s2), .B0(and_by_one_6_b0), .A0(adder_subtractor_7_s1),
    .Over_Flow(adder_subtractor_6_over_flow), .S15(adder_subtractor_6_s15), .S14(adder_subtractor_6_s14),
    .S13(adder_subtractor_6_s13), .S12(adder_subtractor_6_s12), .S11(adder_subtractor_6_s11),
    .S10(adder_subtractor_6_s10), .S9(adder_subtractor_6_s9), .S8(adder_subtractor_6_s8),
    .S7(adder_subtractor_6_s7), .S6(adder_subtractor_6_s6), .S5(adder_subtractor_6_s5),
    .S4(adder_subtractor_6_s4), .S3(adder_subtractor_6_s3), .S2(adder_subtractor_6_s2),
    .S1(adder_subtractor_6_s1), .S0(C10));
  Adder___Subtractor adder_subtractor_7 (
    .M(1'b0), .B15(and_by_one_7_b15), .A15(adder_subtractor_8_over_flow), .B14(and_by_one_7_b14),
    .A14(adder_subtractor_8_s15), .B13(and_by_one_7_b13), .A13(adder_subtractor_8_s14),
    .B12(and_by_one_7_b12), .A12(adder_subtractor_8_s13), .B11(and_by_one_7_b11),
    .A11(adder_subtractor_8_s12), .B10(and_by_one_7_b10), .A10(adder_subtractor_8_s11), .B9(and_by_one_7_b9),
    .A9(adder_subtractor_8_s10), .B8(and_by_one_7_b8), .A8(adder_subtractor_8_s9), .B7(and_by_one_7_b7),
    .A7(adder_subtractor_8_s8), .B6(and_by_one_7_b6), .A6(adder_subtractor_8_s7), .B5(and_by_one_7_b5),
    .A5(adder_subtractor_8_s6), .B4(and_by_one_7_b4), .A4(adder_subtractor_8_s5), .B3(and_by_one_7_b3),
    .A3(adder_subtractor_8_s4), .B2(and_by_one_7_b2), .A2(adder_subtractor_8_s3), .B1(and_by_one_7_b1),
    .A1(adder_subtractor_8_s2), .B0(and_by_one_7_b0), .A0(adder_subtractor_8_s1),
    .Over_Flow(adder_subtractor_7_over_flow), .S15(adder_subtractor_7_s15), .S14(adder_subtractor_7_s14),
    .S13(adder_subtractor_7_s13), .S12(adder_subtractor_7_s12), .S11(adder_subtractor_7_s11),
    .S10(adder_subtractor_7_s10), .S9(adder_subtractor_7_s9), .S8(adder_subtractor_7_s8),
    .S7(adder_subtractor_7_s7), .S6(adder_subtractor_7_s6), .S5(adder_subtractor_7_s5),
    .S4(adder_subtractor_7_s4), .S3(adder_subtractor_7_s3), .S2(adder_subtractor_7_s2),
    .S1(adder_subtractor_7_s1), .S0(C9));
  And_By_one and_by_one_9 (
    .Input(A7_2), .A15(A15), .A14(A14), .A13(A13), .A12(A12), .A11(A11), .A10(A10), .A9(A9), .A8(A8),
    .A7(A7), .A6(A6), .A5(A5), .A4(A4), .A3(A3), .A2(A2), .A1(A1), .A0(A0), .B15(and_by_one_9_b15),
    .B14(and_by_one_9_b14), .B13(and_by_one_9_b13), .B12(and_by_one_9_b12), .B11(and_by_one_9_b11),
    .B10(and_by_one_9_b10), .B9(and_by_one_9_b9), .B8(and_by_one_9_b8), .B7(and_by_one_9_b7),
    .B6(and_by_one_9_b6), .B5(and_by_one_9_b5), .B4(and_by_one_9_b4), .B3(and_by_one_9_b3),
    .B2(and_by_one_9_b2), .B1(and_by_one_9_b1), .B0(and_by_one_9_b0));
  And_By_one and_by_one_10 (
    .Input(A6_2), .A15(A15), .A14(A14), .A13(A13), .A12(A12), .A11(A11), .A10(A10), .A9(A9), .A8(A8),
    .A7(A7), .A6(A6), .A5(A5), .A4(A4), .A3(A3), .A2(A2), .A1(A1), .A0(A0), .B15(and_by_one_10_b15),
    .B14(and_by_one_10_b14), .B13(and_by_one_10_b13), .B12(and_by_one_10_b12), .B11(and_by_one_10_b11),
    .B10(and_by_one_10_b10), .B9(and_by_one_10_b9), .B8(and_by_one_10_b8), .B7(and_by_one_10_b7),
    .B6(and_by_one_10_b6), .B5(and_by_one_10_b5), .B4(and_by_one_10_b4), .B3(and_by_one_10_b3),
    .B2(and_by_one_10_b2), .B1(and_by_one_10_b1), .B0(and_by_one_10_b0));
  Adder___Subtractor adder_subtractor_8 (
    .M(1'b0), .B15(and_by_one_8_b15), .A15(adder_subtractor_9_over_flow), .B14(and_by_one_8_b14),
    .A14(adder_subtractor_9_s15), .B13(and_by_one_8_b13), .A13(adder_subtractor_9_s14),
    .B12(and_by_one_8_b12), .A12(adder_subtractor_9_s13), .B11(and_by_one_8_b11),
    .A11(adder_subtractor_9_s12), .B10(and_by_one_8_b10), .A10(adder_subtractor_9_s11), .B9(and_by_one_8_b9),
    .A9(adder_subtractor_9_s10), .B8(and_by_one_8_b8), .A8(adder_subtractor_9_s9), .B7(and_by_one_8_b7),
    .A7(adder_subtractor_9_s8), .B6(and_by_one_8_b6), .A6(adder_subtractor_9_s7), .B5(and_by_one_8_b5),
    .A5(adder_subtractor_9_s6), .B4(and_by_one_8_b4), .A4(adder_subtractor_9_s5), .B3(and_by_one_8_b3),
    .A3(adder_subtractor_9_s4), .B2(and_by_one_8_b2), .A2(adder_subtractor_9_s3), .B1(and_by_one_8_b1),
    .A1(adder_subtractor_9_s2), .B0(and_by_one_8_b0), .A0(adder_subtractor_9_s1),
    .Over_Flow(adder_subtractor_8_over_flow), .S15(adder_subtractor_8_s15), .S14(adder_subtractor_8_s14),
    .S13(adder_subtractor_8_s13), .S12(adder_subtractor_8_s12), .S11(adder_subtractor_8_s11),
    .S10(adder_subtractor_8_s10), .S9(adder_subtractor_8_s9), .S8(adder_subtractor_8_s8),
    .S7(adder_subtractor_8_s7), .S6(adder_subtractor_8_s6), .S5(adder_subtractor_8_s5),
    .S4(adder_subtractor_8_s4), .S3(adder_subtractor_8_s3), .S2(adder_subtractor_8_s2),
    .S1(adder_subtractor_8_s1), .S0(C8));
  And_By_one and_by_one_11 (
    .Input(A5_2), .A15(A15), .A14(A14), .A13(A13), .A12(A12), .A11(A11), .A10(A10), .A9(A9), .A8(A8),
    .A7(A7), .A6(A6), .A5(A5), .A4(A4), .A3(A3), .A2(A2), .A1(A1), .A0(A0), .B15(and_by_one_11_b15),
    .B14(and_by_one_11_b14), .B13(and_by_one_11_b13), .B12(and_by_one_11_b12), .B11(and_by_one_11_b11),
    .B10(and_by_one_11_b10), .B9(and_by_one_11_b9), .B8(and_by_one_11_b8), .B7(and_by_one_11_b7),
    .B6(and_by_one_11_b6), .B5(and_by_one_11_b5), .B4(and_by_one_11_b4), .B3(and_by_one_11_b3),
    .B2(and_by_one_11_b2), .B1(and_by_one_11_b1), .B0(and_by_one_11_b0));
  Adder___Subtractor adder_subtractor_9 (
    .M(1'b0), .B15(and_by_one_9_b15), .A15(adder_subtractor_10_over_flow), .B14(and_by_one_9_b14),
    .A14(adder_subtractor_10_s15), .B13(and_by_one_9_b13), .A13(adder_subtractor_10_s14),
    .B12(and_by_one_9_b12), .A12(adder_subtractor_10_s13), .B11(and_by_one_9_b11),
    .A11(adder_subtractor_10_s12), .B10(and_by_one_9_b10), .A10(adder_subtractor_10_s11),
    .B9(and_by_one_9_b9), .A9(adder_subtractor_10_s10), .B8(and_by_one_9_b8), .A8(adder_subtractor_10_s9),
    .B7(and_by_one_9_b7), .A7(adder_subtractor_10_s8), .B6(and_by_one_9_b6), .A6(adder_subtractor_10_s7),
    .B5(and_by_one_9_b5), .A5(adder_subtractor_10_s6), .B4(and_by_one_9_b4), .A4(adder_subtractor_10_s5),
    .B3(and_by_one_9_b3), .A3(adder_subtractor_10_s4), .B2(and_by_one_9_b2), .A2(adder_subtractor_10_s3),
    .B1(and_by_one_9_b1), .A1(adder_subtractor_10_s2), .B0(and_by_one_9_b0), .A0(adder_subtractor_10_s1),
    .Over_Flow(adder_subtractor_9_over_flow), .S15(adder_subtractor_9_s15), .S14(adder_subtractor_9_s14),
    .S13(adder_subtractor_9_s13), .S12(adder_subtractor_9_s12), .S11(adder_subtractor_9_s11),
    .S10(adder_subtractor_9_s10), .S9(adder_subtractor_9_s9), .S8(adder_subtractor_9_s8),
    .S7(adder_subtractor_9_s7), .S6(adder_subtractor_9_s6), .S5(adder_subtractor_9_s5),
    .S4(adder_subtractor_9_s4), .S3(adder_subtractor_9_s3), .S2(adder_subtractor_9_s2),
    .S1(adder_subtractor_9_s1), .S0(C7));
  And_By_one and_by_one_12 (
    .Input(A4_2), .A15(A15), .A14(A14), .A13(A13), .A12(A12), .A11(A11), .A10(A10), .A9(A9), .A8(A8),
    .A7(A7), .A6(A6), .A5(A5), .A4(A4), .A3(A3), .A2(A2), .A1(A1), .A0(A0), .B15(and_by_one_12_b15),
    .B14(and_by_one_12_b14), .B13(and_by_one_12_b13), .B12(and_by_one_12_b12), .B11(and_by_one_12_b11),
    .B10(and_by_one_12_b10), .B9(and_by_one_12_b9), .B8(and_by_one_12_b8), .B7(and_by_one_12_b7),
    .B6(and_by_one_12_b6), .B5(and_by_one_12_b5), .B4(and_by_one_12_b4), .B3(and_by_one_12_b3),
    .B2(and_by_one_12_b2), .B1(and_by_one_12_b1), .B0(and_by_one_12_b0));
  Adder___Subtractor adder_subtractor_10 (
    .M(1'b0), .B15(and_by_one_10_b15), .A15(adder_subtractor_11_over_flow), .B14(and_by_one_10_b14),
    .A14(adder_subtractor_11_s15), .B13(and_by_one_10_b13), .A13(adder_subtractor_11_s14),
    .B12(and_by_one_10_b12), .A12(adder_subtractor_11_s13), .B11(and_by_one_10_b11),
    .A11(adder_subtractor_11_s12), .B10(and_by_one_10_b10), .A10(adder_subtractor_11_s11),
    .B9(and_by_one_10_b9), .A9(adder_subtractor_11_s10), .B8(and_by_one_10_b8), .A8(adder_subtractor_11_s9),
    .B7(and_by_one_10_b7), .A7(adder_subtractor_11_s8), .B6(and_by_one_10_b6), .A6(adder_subtractor_11_s7),
    .B5(and_by_one_10_b5), .A5(adder_subtractor_11_s6), .B4(and_by_one_10_b4), .A4(adder_subtractor_11_s5),
    .B3(and_by_one_10_b3), .A3(adder_subtractor_11_s4), .B2(and_by_one_10_b2), .A2(adder_subtractor_11_s3),
    .B1(and_by_one_10_b1), .A1(adder_subtractor_11_s2), .B0(and_by_one_10_b0), .A0(adder_subtractor_11_s1),
    .Over_Flow(adder_subtractor_10_over_flow), .S15(adder_subtractor_10_s15), .S14(adder_subtractor_10_s14),
    .S13(adder_subtractor_10_s13), .S12(adder_subtractor_10_s12), .S11(adder_subtractor_10_s11),
    .S10(adder_subtractor_10_s10), .S9(adder_subtractor_10_s9), .S8(adder_subtractor_10_s8),
    .S7(adder_subtractor_10_s7), .S6(adder_subtractor_10_s6), .S5(adder_subtractor_10_s5),
    .S4(adder_subtractor_10_s4), .S3(adder_subtractor_10_s3), .S2(adder_subtractor_10_s2),
    .S1(adder_subtractor_10_s1), .S0(C6));
  And_By_one and_by_one_13 (
    .Input(A3_2), .A15(A15), .A14(A14), .A13(A13), .A12(A12), .A11(A11), .A10(A10), .A9(A9), .A8(A8),
    .A7(A7), .A6(A6), .A5(A5), .A4(A4), .A3(A3), .A2(A2), .A1(A1), .A0(A0), .B15(and_by_one_13_b15),
    .B14(and_by_one_13_b14), .B13(and_by_one_13_b13), .B12(and_by_one_13_b12), .B11(and_by_one_13_b11),
    .B10(and_by_one_13_b10), .B9(and_by_one_13_b9), .B8(and_by_one_13_b8), .B7(and_by_one_13_b7),
    .B6(and_by_one_13_b6), .B5(and_by_one_13_b5), .B4(and_by_one_13_b4), .B3(and_by_one_13_b3),
    .B2(and_by_one_13_b2), .B1(and_by_one_13_b1), .B0(and_by_one_13_b0));
  Adder___Subtractor adder_subtractor_11 (
    .M(1'b0), .B15(and_by_one_11_b15), .A15(adder_subtractor_12_over_flow), .B14(and_by_one_11_b14),
    .A14(adder_subtractor_12_s15), .B13(and_by_one_11_b13), .A13(adder_subtractor_12_s14),
    .B12(and_by_one_11_b12), .A12(adder_subtractor_12_s13), .B11(and_by_one_11_b11),
    .A11(adder_subtractor_12_s12), .B10(and_by_one_11_b10), .A10(adder_subtractor_12_s11),
    .B9(and_by_one_11_b9), .A9(adder_subtractor_12_s10), .B8(and_by_one_11_b8), .A8(adder_subtractor_12_s9),
    .B7(and_by_one_11_b7), .A7(adder_subtractor_12_s8), .B6(and_by_one_11_b6), .A6(adder_subtractor_12_s7),
    .B5(and_by_one_11_b5), .A5(adder_subtractor_12_s6), .B4(and_by_one_11_b4), .A4(adder_subtractor_12_s5),
    .B3(and_by_one_11_b3), .A3(adder_subtractor_12_s4), .B2(and_by_one_11_b2), .A2(adder_subtractor_12_s3),
    .B1(and_by_one_11_b1), .A1(adder_subtractor_12_s2), .B0(and_by_one_11_b0), .A0(adder_subtractor_12_s1),
    .Over_Flow(adder_subtractor_11_over_flow), .S15(adder_subtractor_11_s15), .S14(adder_subtractor_11_s14),
    .S13(adder_subtractor_11_s13), .S12(adder_subtractor_11_s12), .S11(adder_subtractor_11_s11),
    .S10(adder_subtractor_11_s10), .S9(adder_subtractor_11_s9), .S8(adder_subtractor_11_s8),
    .S7(adder_subtractor_11_s7), .S6(adder_subtractor_11_s6), .S5(adder_subtractor_11_s5),
    .S4(adder_subtractor_11_s4), .S3(adder_subtractor_11_s3), .S2(adder_subtractor_11_s2),
    .S1(adder_subtractor_11_s1), .S0(C5));
  And_By_one and_by_one_14 (
    .Input(A2_2), .A15(A15), .A14(A14), .A13(A13), .A12(A12), .A11(A11), .A10(A10), .A9(A9), .A8(A8),
    .A7(A7), .A6(A6), .A5(A5), .A4(A4), .A3(A3), .A2(A2), .A1(A1), .A0(A0), .B15(and_by_one_14_b15),
    .B14(and_by_one_14_b14), .B13(and_by_one_14_b13), .B12(and_by_one_14_b12), .B11(and_by_one_14_b11),
    .B10(and_by_one_14_b10), .B9(and_by_one_14_b9), .B8(and_by_one_14_b8), .B7(and_by_one_14_b7),
    .B6(and_by_one_14_b6), .B5(and_by_one_14_b5), .B4(and_by_one_14_b4), .B3(and_by_one_14_b3),
    .B2(and_by_one_14_b2), .B1(and_by_one_14_b1), .B0(and_by_one_14_b0));
  Adder___Subtractor adder_subtractor_12 (
    .M(1'b0), .B15(and_by_one_12_b15), .A15(adder_subtractor_13_over_flow), .B14(and_by_one_12_b14),
    .A14(adder_subtractor_13_s15), .B13(and_by_one_12_b13), .A13(adder_subtractor_13_s14),
    .B12(and_by_one_12_b12), .A12(adder_subtractor_13_s13), .B11(and_by_one_12_b11),
    .A11(adder_subtractor_13_s12), .B10(and_by_one_12_b10), .A10(adder_subtractor_13_s11),
    .B9(and_by_one_12_b9), .A9(adder_subtractor_13_s10), .B8(and_by_one_12_b8), .A8(adder_subtractor_13_s9),
    .B7(and_by_one_12_b7), .A7(adder_subtractor_13_s8), .B6(and_by_one_12_b6), .A6(adder_subtractor_13_s7),
    .B5(and_by_one_12_b5), .A5(adder_subtractor_13_s6), .B4(and_by_one_12_b4), .A4(adder_subtractor_13_s5),
    .B3(and_by_one_12_b3), .A3(adder_subtractor_13_s4), .B2(and_by_one_12_b2), .A2(adder_subtractor_13_s3),
    .B1(and_by_one_12_b1), .A1(adder_subtractor_13_s2), .B0(and_by_one_12_b0), .A0(adder_subtractor_13_s1),
    .Over_Flow(adder_subtractor_12_over_flow), .S15(adder_subtractor_12_s15), .S14(adder_subtractor_12_s14),
    .S13(adder_subtractor_12_s13), .S12(adder_subtractor_12_s12), .S11(adder_subtractor_12_s11),
    .S10(adder_subtractor_12_s10), .S9(adder_subtractor_12_s9), .S8(adder_subtractor_12_s8),
    .S7(adder_subtractor_12_s7), .S6(adder_subtractor_12_s6), .S5(adder_subtractor_12_s5),
    .S4(adder_subtractor_12_s4), .S3(adder_subtractor_12_s3), .S2(adder_subtractor_12_s2),
    .S1(adder_subtractor_12_s1), .S0(C4));
  And_By_one and_by_one_15 (
    .Input(A1_2), .A15(A15), .A14(A14), .A13(A13), .A12(A12), .A11(A11), .A10(A10), .A9(A9), .A8(A8),
    .A7(A7), .A6(A6), .A5(A5), .A4(A4), .A3(A3), .A2(A2), .A1(A1), .A0(A0), .B15(and_by_one_15_b15),
    .B14(and_by_one_15_b14), .B13(and_by_one_15_b13), .B12(and_by_one_15_b12), .B11(and_by_one_15_b11),
    .B10(and_by_one_15_b10), .B9(and_by_one_15_b9), .B8(and_by_one_15_b8), .B7(and_by_one_15_b7),
    .B6(and_by_one_15_b6), .B5(and_by_one_15_b5), .B4(and_by_one_15_b4), .B3(and_by_one_15_b3),
    .B2(and_by_one_15_b2), .B1(and_by_one_15_b1), .B0(and_by_one_15_b0));
  Adder___Subtractor adder_subtractor_13 (
    .M(1'b0), .B15(and_by_one_13_b15), .A15(adder_subtractor_14_over_flow), .B14(and_by_one_13_b14),
    .A14(adder_subtractor_14_s15), .B13(and_by_one_13_b13), .A13(adder_subtractor_14_s14),
    .B12(and_by_one_13_b12), .A12(adder_subtractor_14_s13), .B11(and_by_one_13_b11),
    .A11(adder_subtractor_14_s12), .B10(and_by_one_13_b10), .A10(adder_subtractor_14_s11),
    .B9(and_by_one_13_b9), .A9(adder_subtractor_14_s10), .B8(and_by_one_13_b8), .A8(adder_subtractor_14_s9),
    .B7(and_by_one_13_b7), .A7(adder_subtractor_14_s8), .B6(and_by_one_13_b6), .A6(adder_subtractor_14_s7),
    .B5(and_by_one_13_b5), .A5(adder_subtractor_14_s6), .B4(and_by_one_13_b4), .A4(adder_subtractor_14_s5),
    .B3(and_by_one_13_b3), .A3(adder_subtractor_14_s4), .B2(and_by_one_13_b2), .A2(adder_subtractor_14_s3),
    .B1(and_by_one_13_b1), .A1(adder_subtractor_14_s2), .B0(and_by_one_13_b0), .A0(adder_subtractor_14_s1),
    .Over_Flow(adder_subtractor_13_over_flow), .S15(adder_subtractor_13_s15), .S14(adder_subtractor_13_s14),
    .S13(adder_subtractor_13_s13), .S12(adder_subtractor_13_s12), .S11(adder_subtractor_13_s11),
    .S10(adder_subtractor_13_s10), .S9(adder_subtractor_13_s9), .S8(adder_subtractor_13_s8),
    .S7(adder_subtractor_13_s7), .S6(adder_subtractor_13_s6), .S5(adder_subtractor_13_s5),
    .S4(adder_subtractor_13_s4), .S3(adder_subtractor_13_s3), .S2(adder_subtractor_13_s2),
    .S1(adder_subtractor_13_s1), .S0(C3));
  Adder___Subtractor adder_subtractor_14 (
    .M(1'b0), .B15(and_by_one_14_b15), .A15(adder_subtractor_15_over_flow), .B14(and_by_one_14_b14),
    .A14(adder_subtractor_15_s15), .B13(and_by_one_14_b13), .A13(adder_subtractor_15_s14),
    .B12(and_by_one_14_b12), .A12(adder_subtractor_15_s13), .B11(and_by_one_14_b11),
    .A11(adder_subtractor_15_s12), .B10(and_by_one_14_b10), .A10(adder_subtractor_15_s11),
    .B9(and_by_one_14_b9), .A9(adder_subtractor_15_s10), .B8(and_by_one_14_b8), .A8(adder_subtractor_15_s9),
    .B7(and_by_one_14_b7), .A7(adder_subtractor_15_s8), .B6(and_by_one_14_b6), .A6(adder_subtractor_15_s7),
    .B5(and_by_one_14_b5), .A5(adder_subtractor_15_s6), .B4(and_by_one_14_b4), .A4(adder_subtractor_15_s5),
    .B3(and_by_one_14_b3), .A3(adder_subtractor_15_s4), .B2(and_by_one_14_b2), .A2(adder_subtractor_15_s3),
    .B1(and_by_one_14_b1), .A1(adder_subtractor_15_s2), .B0(and_by_one_14_b0), .A0(adder_subtractor_15_s1),
    .Over_Flow(adder_subtractor_14_over_flow), .S15(adder_subtractor_14_s15), .S14(adder_subtractor_14_s14),
    .S13(adder_subtractor_14_s13), .S12(adder_subtractor_14_s12), .S11(adder_subtractor_14_s11),
    .S10(adder_subtractor_14_s10), .S9(adder_subtractor_14_s9), .S8(adder_subtractor_14_s8),
    .S7(adder_subtractor_14_s7), .S6(adder_subtractor_14_s6), .S5(adder_subtractor_14_s5),
    .S4(adder_subtractor_14_s4), .S3(adder_subtractor_14_s3), .S2(adder_subtractor_14_s2),
    .S1(adder_subtractor_14_s1), .S0(C2));
  Adder___Subtractor adder_subtractor_15 (
    .M(1'b0), .B15(and_by_one_15_b15), .A15(1'b0), .B14(and_by_one_15_b14), .A14(and_by_one_16_b15),
    .B13(and_by_one_15_b13), .A13(and_by_one_16_b14), .B12(and_by_one_15_b12), .A12(and_by_one_16_b13),
    .B11(and_by_one_15_b11), .A11(and_by_one_16_b12), .B10(and_by_one_15_b10), .A10(and_by_one_16_b11),
    .B9(and_by_one_15_b9), .A9(and_by_one_16_b10), .B8(and_by_one_15_b8), .A8(and_by_one_16_b9),
    .B7(and_by_one_15_b7), .A7(and_by_one_16_b8), .B6(and_by_one_15_b6), .A6(and_by_one_16_b7),
    .B5(and_by_one_15_b5), .A5(and_by_one_16_b6), .B4(and_by_one_15_b4), .A4(and_by_one_16_b5),
    .B3(and_by_one_15_b3), .A3(and_by_one_16_b4), .B2(and_by_one_15_b2), .A2(and_by_one_16_b3),
    .B1(and_by_one_15_b1), .A1(and_by_one_16_b2), .B0(and_by_one_15_b0), .A0(and_by_one_16_b1),
    .Over_Flow(adder_subtractor_15_over_flow), .S15(adder_subtractor_15_s15), .S14(adder_subtractor_15_s14),
    .S13(adder_subtractor_15_s13), .S12(adder_subtractor_15_s12), .S11(adder_subtractor_15_s11),
    .S10(adder_subtractor_15_s10), .S9(adder_subtractor_15_s9), .S8(adder_subtractor_15_s8),
    .S7(adder_subtractor_15_s7), .S6(adder_subtractor_15_s6), .S5(adder_subtractor_15_s5),
    .S4(adder_subtractor_15_s4), .S3(adder_subtractor_15_s3), .S2(adder_subtractor_15_s2),
    .S1(adder_subtractor_15_s1), .S0(C1));
  And_By_one and_by_one_16 (
    .Input(A0_2), .A15(A15), .A14(A14), .A13(A13), .A12(A12), .A11(A11), .A10(A10), .A9(A9), .A8(A8),
    .A7(A7), .A6(A6), .A5(A5), .A4(A4), .A3(A3), .A2(A2), .A1(A1), .A0(A0), .B15(and_by_one_16_b15),
    .B14(and_by_one_16_b14), .B13(and_by_one_16_b13), .B12(and_by_one_16_b12), .B11(and_by_one_16_b11),
    .B10(and_by_one_16_b10), .B9(and_by_one_16_b9), .B8(and_by_one_16_b8), .B7(and_by_one_16_b7),
    .B6(and_by_one_16_b6), .B5(and_by_one_16_b5), .B4(and_by_one_16_b4), .B3(and_by_one_16_b3),
    .B2(and_by_one_16_b2), .B1(and_by_one_16_b1), .B0(C0));
endmodule

module And_By_one (
  input  A15,
  input  A14,
  input  A13,
  input  A12,
  input  A11,
  input  A10,
  input  A9,
  input  A8,
  input  A7,
  input  A6,
  input  A5,
  input  A4,
  input  A3,
  input  A2,
  input  A1,
  input  A0,
  input  Input,
  output B15,
  output B14,
  output B13,
  output B12,
  output B11,
  output B10,
  output B9,
  output B8,
  output B7,
  output B6,
  output B5,
  output B4,
  output B3,
  output B2,
  output B1,
  output B0
);

  and and_1 (B14, A14, Input);
  and and_2 (B15, A15, Input);
  and and_3 (B12, A12, Input);
  and and_4 (B13, A13, Input);
  and and_5 (B10, A10, Input);
  and and_6 (B11, A11, Input);
  and and_7 (B9, A9, Input);
  and and_8 (B8, A8, Input);
  and and_9 (B6, A6, Input);
  and and_10 (B7, A7, Input);
  and and_11 (B5, A5, Input);
  and and_12 (B4, A4, Input);
  and and_13 (B2, A2, Input);
  and and_14 (B3, A3, Input);
  and and_15 (B0, A0, Input);
  and and_16 (B1, A1, Input);
endmodule

module Adder_by_1 (
  input  A15,
  input  A14,
  input  A13,
  input  A12,
  input  A11,
  input  A10,
  input  A9,
  input  A8,
  input  A7,
  input  A6,
  input  A5,
  input  A4,
  input  A3,
  input  A2,
  input  A1,
  input  A0,
  input  E,
  output Over_Flow,
  output B15,
  output B14,
  output B13,
  output B12,
  output B11,
  output B10,
  output B9,
  output B8,
  output B7,
  output B6,
  output B5,
  output B4,
  output B3,
  output B2,
  output B1,
  output B0
);

  wire adder_subtractor_1_over_flow, adder_subtractor_1_s0, adder_subtractor_1_s1, adder_subtractor_1_s2,
       adder_subtractor_1_s3, adder_subtractor_1_s4, adder_subtractor_1_s5, adder_subtractor_1_s6,
       adder_subtractor_1_s7, adder_subtractor_1_s8, adder_subtractor_1_s9, adder_subtractor_1_s10,
       adder_subtractor_1_s11, adder_subtractor_1_s12, adder_subtractor_1_s13, adder_subtractor_1_s14,
       adder_subtractor_1_s15;

  and and_1 (Over_Flow, E, adder_subtractor_1_over_flow);
  And_By_one and_by_one_1 (
    .Input(E), .A15(adder_subtractor_1_s15), .A14(adder_subtractor_1_s14), .A13(adder_subtractor_1_s13),
    .A12(adder_subtractor_1_s12), .A11(adder_subtractor_1_s11), .A10(adder_subtractor_1_s10),
    .A9(adder_subtractor_1_s9), .A8(adder_subtractor_1_s8), .A7(adder_subtractor_1_s7),
    .A6(adder_subtractor_1_s6), .A5(adder_subtractor_1_s5), .A4(adder_subtractor_1_s4),
    .A3(adder_subtractor_1_s3), .A2(adder_subtractor_1_s2), .A1(adder_subtractor_1_s1),
    .A0(adder_subtractor_1_s0), .B15(B15), .B14(B14), .B13(B13), .B12(B12), .B11(B11), .B10(B10), .B9(B9),
    .B8(B8), .B7(B7), .B6(B6), .B5(B5), .B4(B4), .B3(B3), .B2(B2), .B1(B1), .B0(B0));
  Adder___Subtractor adder_subtractor_1 (
    .M(1'b0), .B15(1'b0), .A15(A15), .B14(1'b0), .A14(A14), .B13(1'b0), .A13(A13), .B12(1'b0), .A12(A12),
    .B11(1'b0), .A11(A11), .B10(1'b0), .A10(A10), .B9(1'b0), .A9(A9), .B8(1'b0), .A8(A8), .B7(1'b0), .A7(A7),
    .B6(1'b0), .A6(A6), .B5(1'b0), .A5(A5), .B4(1'b0), .A4(A4), .B3(1'b0), .A3(A3), .B2(1'b0), .A2(A2),
    .B1(1'b0), .A1(A1), .B0(1'b1), .A0(A0), .Over_Flow(adder_subtractor_1_over_flow),
    .S15(adder_subtractor_1_s15), .S14(adder_subtractor_1_s14), .S13(adder_subtractor_1_s13),
    .S12(adder_subtractor_1_s12), .S11(adder_subtractor_1_s11), .S10(adder_subtractor_1_s10),
    .S9(adder_subtractor_1_s9), .S8(adder_subtractor_1_s8), .S7(adder_subtractor_1_s7),
    .S6(adder_subtractor_1_s6), .S5(adder_subtractor_1_s5), .S4(adder_subtractor_1_s4),
    .S3(adder_subtractor_1_s3), .S2(adder_subtractor_1_s2), .S1(adder_subtractor_1_s1),
    .S0(adder_subtractor_1_s0));
endmodule

module Test_Gates (
);

  wire undriven, undriven_2, undriven_3, undriven_4, undriven_5, undriven_6;

  Multiplier_16Bit multiplier_16bit_1 (
    .A15_2(undriven), .A14_2(undriven_3), .A13_2(undriven_2), .A12_2(undriven_4), .A11_2(undriven_5),
    .A10_2(undriven_6));  // open: A15, A14, A13, A12, A11, A10, A9, A8, A7, A6, A5, A4, A3, A2, A1, A0, A9_2, A8_2, A7_2, A6_2, A5_2, A4_2, A3_2, A2_2, A1_2, A0_2, C31, C30, C29, C28, C27, C26, C25, C24, C23, C22, C21, C20, C19, C18, C17, C16, C15, C14, C13, C12, C11, C10, C9, C8, C7, C6, C5, C4, C3, C2, C1, C0
endmodule

module Subtractor_by_1 (
  input  A15,
  input  A14,
  input  A13,
  input  A12,
  input  A11,
  input  A10,
  input  A9,
  input  A8,
  input  A7,
  input  A6,
  input  A5,
  input  A4,
  input  A3,
  input  A2,
  input  A1,
  input  A0,
  input  E,
  output Over_Flow,
  output B15,
  output B14,
  output B13,
  output B12,
  output B11,
  output B10,
  output B9,
  output B8,
  output B7,
  output B5,
  output B4,
  output B3,
  output B2,
  output B1,
  output B0,
  output B6
);

  wire adder_subtractor_1_over_flow, adder_subtractor_1_s0, adder_subtractor_1_s1, adder_subtractor_1_s2,
       adder_subtractor_1_s3, adder_subtractor_1_s4, adder_subtractor_1_s5, adder_subtractor_1_s6,
       adder_subtractor_1_s7, adder_subtractor_1_s8, adder_subtractor_1_s9, adder_subtractor_1_s10,
       adder_subtractor_1_s11, adder_subtractor_1_s12, adder_subtractor_1_s13, adder_subtractor_1_s14,
       adder_subtractor_1_s15;

  and and_1 (Over_Flow, E, adder_subtractor_1_over_flow);
  And_By_one and_by_one_1 (
    .Input(E), .A15(adder_subtractor_1_s15), .A14(adder_subtractor_1_s14), .A13(adder_subtractor_1_s13),
    .A12(adder_subtractor_1_s12), .A11(adder_subtractor_1_s11), .A10(adder_subtractor_1_s10),
    .A9(adder_subtractor_1_s9), .A8(adder_subtractor_1_s8), .A7(adder_subtractor_1_s7),
    .A6(adder_subtractor_1_s6), .A5(adder_subtractor_1_s5), .A4(adder_subtractor_1_s4),
    .A3(adder_subtractor_1_s3), .A2(adder_subtractor_1_s2), .A1(adder_subtractor_1_s1),
    .A0(adder_subtractor_1_s0), .B15(B15), .B14(B14), .B13(B13), .B12(B12), .B11(B11), .B10(B10), .B9(B9),
    .B8(B8), .B7(B7), .B6(B6), .B5(B5), .B4(B4), .B3(B3), .B2(B2), .B1(B1), .B0(B0));
  Adder___Subtractor adder_subtractor_1 (
    .M(1'b1), .B15(1'b0), .A15(A15), .B14(1'b0), .A14(A14), .B13(1'b0), .A13(A13), .B12(1'b0), .A12(A12),
    .B11(1'b0), .A11(A11), .B10(1'b0), .A10(A10), .B9(1'b0), .A9(A9), .B8(1'b0), .A8(A8), .B7(1'b0), .A7(A7),
    .B6(1'b0), .A6(A6), .B5(1'b0), .A5(A5), .B4(1'b0), .A4(A4), .B3(1'b0), .A3(A3), .B2(1'b0), .A2(A2),
    .B1(1'b0), .A1(A1), .B0(1'b1), .A0(A0), .Over_Flow(adder_subtractor_1_over_flow),
    .S15(adder_subtractor_1_s15), .S14(adder_subtractor_1_s14), .S13(adder_subtractor_1_s13),
    .S12(adder_subtractor_1_s12), .S11(adder_subtractor_1_s11), .S10(adder_subtractor_1_s10),
    .S9(adder_subtractor_1_s9), .S8(adder_subtractor_1_s8), .S7(adder_subtractor_1_s7),
    .S6(adder_subtractor_1_s6), .S5(adder_subtractor_1_s5), .S4(adder_subtractor_1_s4),
    .S3(adder_subtractor_1_s3), .S2(adder_subtractor_1_s2), .S1(adder_subtractor_1_s1),
    .S0(adder_subtractor_1_s0));
endmodule

module And (
  input  B15,
  input  B14,
  input  B13,
  input  B12,
  input  B11,
  input  B10,
  input  B9,
  input  B8,
  input  B7,
  input  B6,
  input  B5,
  input  B4,
  input  B3,
  input  B2,
  input  B1,
  input  B0,
  input  A15,
  input  A14,
  input  A13,
  input  A12,
  input  A11,
  input  A10,
  input  A9,
  input  A8,
  input  A7,
  input  A6,
  input  A5,
  input  A4,
  input  A3,
  input  A2,
  input  A1,
  input  A0,
  input  E,
  output C15,
  output C14,
  output C13,
  output C12,
  output C11,
  output C10,
  output C9,
  output C8,
  output C7,
  output C6,
  output C5,
  output C4,
  output C3,
  output C2,
  output C1,
  output C0
);

  wire and_1_out, and_3_out, and_4_out, and_7_out, and_8_out, and_11_out, and_12_out, and_15_out, and_16_out,
       and_19_out, and_20_out, and_23_out, and_24_out, and_27_out, and_28_out, and_31_out;

  and and_1 (and_1_out, B15, A15);
  and and_2 (C15, E, and_1_out);
  and and_3 (and_3_out, B13, A13);
  and and_4 (and_4_out, B14, A14);
  and and_5 (C13, E, and_3_out);
  and and_6 (C14, E, and_4_out);
  and and_7 (and_7_out, B12, A12);
  and and_8 (and_8_out, B11, A11);
  and and_9 (C11, E, and_8_out);
  and and_10 (C12, E, and_7_out);
  and and_11 (and_11_out, B9, A9);
  and and_12 (and_12_out, B10, A10);
  and and_13 (C9, E, and_11_out);
  and and_14 (C10, E, and_12_out);
  and and_15 (and_15_out, B7, A7);
  and and_16 (and_16_out, B8, A8);
  and and_17 (C8, E, and_16_out);
  and and_18 (C7, E, and_15_out);
  and and_19 (and_19_out, B5, A5);
  and and_20 (and_20_out, B6, A6);
  and and_21 (C5, E, and_19_out);
  and and_22 (C6, E, and_20_out);
  and and_23 (and_23_out, B3, A3);
  and and_24 (and_24_out, B4, A4);
  and and_25 (C3, E, and_23_out);
  and and_26 (C4, E, and_24_out);
  and and_27 (and_27_out, B2, A2);
  and and_28 (and_28_out, B1, A1);
  and and_29 (C1, E, and_28_out);
  and and_30 (C2, E, and_27_out);
  and and_31 (and_31_out, B0, A0);
  and and_32 (C0, E, and_31_out);
endmodule

module OR (
  input  B15,
  input  B14,
  input  B13,
  input  B12,
  input  B11,
  input  B10,
  input  B9,
  input  B8,
  input  B7,
  input  B6,
  input  B5,
  input  B4,
  input  B3,
  input  B2,
  input  B1,
  input  B0,
  input  A15,
  input  A14,
  input  A13,
  input  A12,
  input  A11,
  input  A10,
  input  A9,
  input  A8,
  input  A7,
  input  A6,
  input  A5,
  input  A4,
  input  A3,
  input  A2,
  input  A1,
  input  A0,
  input  E,
  output C15,
  output C14,
  output C13,
  output C12,
  output C11,
  output C10,
  output C9,
  output C8,
  output C7,
  output C6,
  output C5,
  output C4,
  output C3,
  output C2,
  output C1,
  output C0
);

  wire or_1_out, or_2_out, or_3_out, or_4_out, or_5_out, or_6_out, or_7_out, or_8_out, or_9_out, or_10_out,
       or_11_out, or_12_out, or_13_out, or_14_out, or_15_out, or_16_out;

  or or_1 (or_1_out, B15, A15);
  and and_1 (C15, E, or_1_out);
  or or_2 (or_2_out, B14, A14);
  or or_3 (or_3_out, B13, A13);
  and and_2 (C13, E, or_3_out);
  and and_3 (C14, E, or_2_out);
  or or_4 (or_4_out, B12, A12);
  or or_5 (or_5_out, B11, A11);
  and and_4 (C12, E, or_4_out);
  and and_5 (C11, E, or_5_out);
  or or_6 (or_6_out, B10, A10);
  or or_7 (or_7_out, B9, A9);
  and and_6 (C10, E, or_6_out);
  and and_7 (C9, E, or_7_out);
  or or_8 (or_8_out, B7, A7);
  or or_9 (or_9_out, B8, A8);
  and and_8 (C7, E, or_8_out);
  and and_9 (C8, E, or_9_out);
  or or_10 (or_10_out, B5, A5);
  or or_11 (or_11_out, B6, A6);
  and and_10 (C6, E, or_11_out);
  and and_11 (C5, E, or_10_out);
  or or_12 (or_12_out, B4, A4);
  or or_13 (or_13_out, B3, A3);
  and and_12 (C4, E, or_12_out);
  and and_13 (C3, E, or_13_out);
  or or_14 (or_14_out, B1, A1);
  or or_15 (or_15_out, B2, A2);
  and and_14 (C2, E, or_15_out);
  and and_15 (C1, E, or_14_out);
  or or_16 (or_16_out, B0, A0);
  and and_16 (C0, E, or_16_out);
endmodule

module XOR (
  input  B15,
  input  B14,
  input  B13,
  input  B12,
  input  B11,
  input  B10,
  input  B9,
  input  B8,
  input  B7,
  input  B6,
  input  B5,
  input  B4,
  input  B3,
  input  B2,
  input  B1,
  input  B0,
  input  A15,
  input  A14,
  input  A13,
  input  A12,
  input  A11,
  input  A10,
  input  A9,
  input  A8,
  input  A7,
  input  A6,
  input  A5,
  input  A4,
  input  A3,
  input  A2,
  input  A1,
  input  A0,
  input  E,
  output C15,
  output C14,
  output C13,
  output C12,
  output C11,
  output C10,
  output C9,
  output C8,
  output C7,
  output C6,
  output C5,
  output C4,
  output C3,
  output C2,
  output C1,
  output C0
);

  wire xor_1_out, xor_2_out, xor_3_out, xor_4_out, xor_5_out, xor_6_out, xor_7_out, xor_8_out, xor_9_out,
       xor_10_out, xor_11_out, xor_12_out, xor_13_out, xor_14_out, xor_15_out, xor_16_out;

  xor xor_1 (xor_1_out, B15, A15);
  and and_1 (C15, E, xor_1_out);
  xor xor_2 (xor_2_out, B14, A14);
  xor xor_3 (xor_3_out, B13, A13);
  and and_2 (C13, E, xor_3_out);
  and and_3 (C14, E, xor_2_out);
  xor xor_4 (xor_4_out, B12, A12);
  xor xor_5 (xor_5_out, B11, A11);
  and and_4 (C12, E, xor_4_out);
  and and_5 (C11, E, xor_5_out);
  xor xor_6 (xor_6_out, B9, A9);
  xor xor_7 (xor_7_out, B10, A10);
  and and_6 (C9, E, xor_6_out);
  and and_7 (C10, E, xor_7_out);
  xor xor_8 (xor_8_out, B7, A7);
  xor xor_9 (xor_9_out, B8, A8);
  and and_8 (C8, E, xor_9_out);
  and and_9 (C7, E, xor_8_out);
  xor xor_10 (xor_10_out, B6, A6);
  xor xor_11 (xor_11_out, B5, A5);
  and and_10 (C6, E, xor_10_out);
  and and_11 (C5, E, xor_11_out);
  xor xor_12 (xor_12_out, B4, A4);
  xor xor_13 (xor_13_out, B3, A3);
  and and_12 (C4, E, xor_12_out);
  and and_13 (C3, E, xor_13_out);
  xor xor_14 (xor_14_out, B2, A2);
  xor xor_15 (xor_15_out, B1, A1);
  and and_14 (C1, E, xor_15_out);
  and and_15 (C2, E, xor_14_out);
  xor xor_16 (xor_16_out, B0, A0);
  and and_16 (C0, E, xor_16_out);
endmodule

module NOT (
  input  A15,
  input  A14,
  input  A13,
  input  A12,
  input  A11,
  input  A10,
  input  A9,
  input  A8,
  input  A7,
  input  A6,
  input  A5,
  input  A4,
  input  A3,
  input  A2,
  input  A1,
  input  A0,
  input  E,
  output B15,
  output B14,
  output B13,
  output B12,
  output B11,
  output B10,
  output B9,
  output B8,
  output B7,
  output B6,
  output B5,
  output B4,
  output B3,
  output B2,
  output B1,
  output B0
);

  and and_1 (B15, A1, ~A1);  // AND_Gate
  and and_2 (B13, A1, ~A1);  // AND_Gate
  and and_3 (B14, A1, ~A1);  // AND_Gate
  and and_4 (B11, A1, ~A1);  // AND_Gate
  and and_5 (B12, A1, ~A1);  // AND_Gate
  and and_6 (B10, A1, ~A1);  // AND_Gate
  and and_7 (B9, A1, ~A1);  // AND_Gate
  and and_8 (B8, A1, ~A1);  // AND_Gate
  and and_9 (B7, A1, ~A1);  // AND_Gate
  and and_10 (B5, A1, ~A1);  // AND_Gate
  and and_11 (B6, A1, ~A1);  // AND_Gate
  and and_12 (B4, A1, ~A1);  // AND_Gate
  and and_13 (B3, A1, ~A1);  // AND_Gate
  and and_14 (B1, A1, ~A1);  // AND_Gate
  and and_15 (B2, A1, ~A1);  // AND_Gate
  and and_16 (B0, A1, ~A0);  // AND_Gate

  assign A2 = A1;
  assign A3 = A1;
  assign A4 = A1;
  assign A5 = A1;
  assign A6 = A1;
  assign A7 = A1;
  assign A8 = A1;
  assign A9 = A1;
  assign A10 = A1;
  assign A11 = A1;
  assign A12 = A1;
  assign A13 = A1;
  assign A14 = A1;
  assign A15 = A1;
  assign E = A1;
endmodule

module SLA (
  input  Rotate,
  input  A15,
  input  A14,
  input  A13,
  input  A12,
  input  A11,
  input  A10,
  input  A9,
  input  A8,
  input  A7,
  input  A6,
  input  A5,
  input  A4,
  input  A3,
  input  A2,
  input  A1,
  input  A0,
  input  E,
  output B15,
  output B14,
  output B13,
  output B12,
  output B11,
  output B10,
  output B9,
  output B8,
  output B7,
  output B6,
  output B5,
  output B4,
  output B3,
  output B2,
  output B1,
  output B0
);

  wire and_16_out;

  and and_1 (B14, E, A13);
  and and_2 (B15, E, A14);
  and and_3 (B13, E, A12);
  and and_4 (B12, E, A11);
  and and_5 (B11, E, A10);
  and and_6 (B10, E, A9);
  and and_7 (B9, E, A8);
  and and_8 (B8, E, A7);
  and and_9 (B7, E, A6);
  and and_10 (B6, E, A5);
  and and_11 (B5, E, A4);
  and and_12 (B3, E, A2);
  and and_13 (B4, E, A3);
  and and_14 (B1, E, A0);
  and and_15 (B2, E, A1);
  and and_16 (and_16_out, Rotate, A15);
  and and_17 (B0, E, and_16_out);
endmodule

module SRA (
  input  Rotate,
  input  A0,
  input  A15,
  input  A14,
  input  A13,
  input  A12,
  input  A11,
  input  A10,
  input  A9,
  input  A8,
  input  A7,
  input  A6,
  input  A5,
  input  A4,
  input  A3,
  input  A2,
  input  A1,
  input  E,
  output B15,
  output B14,
  output B13,
  output B12,
  output B11,
  output B10,
  output B9,
  output B8,
  output B7,
  output B6,
  output B5,
  output B4,
  output B3,
  output B2,
  output B1,
  output B0
);

  wire and_1_out;

  and and_1 (and_1_out, Rotate, A0);
  and and_2 (B14, E, A15);
  and and_3 (B15, E, and_1_out);
  and and_4 (B12, E, A13);
  and and_5 (B13, E, A14);
  and and_6 (B10, E, A11);
  and and_7 (B11, E, A12);
  and and_8 (B9, E, A10);
  and and_9 (B8, E, A9);
  and and_10 (B7, E, A8);
  and and_11 (B5, E, A6);
  and and_12 (B6, E, A7);
  and and_13 (B3, E, A4);
  and and_14 (B4, E, A5);
  and and_15 (B1, E, A2);
  and and_16 (B2, E, A3);
  and and_17 (B0, E, A1);
endmodule

module DEMUX_1_32 (
  input  E,
  input  S4,
  input  S3,
  input  S2,
  input  S1,
  input  S0,
  output A0,
  output A1,
  output A2,
  output A3,
  output A4,
  output A5,
  output A6,
  output A7,
  output A8,
  output A9,
  output A10,
  output A11,
  output A12,
  output A13,
  output A14,
  output A15,
  output A16,
  output A17,
  output A18,
  output A19,
  output A20,
  output A21,
  output A22,
  output A23,
  output A24,
  output A25,
  output A26,
  output A27,
  output A28,
  output A29,
  output A30,
  output A31
);

  wire not_1_out, not_2_out, not_3_out, not_4_out, not_5_out;

  not not_1 (not_1_out, S4);
  not not_2 (not_2_out, S3);
  not not_3 (not_3_out, S2);
  not not_4 (not_4_out, S1);
  not not_5 (not_5_out, S0);
  and and_1 (A0, E, not_1_out, not_2_out, not_3_out, not_4_out, not_5_out);
  and and_2 (A1, E, not_1_out, not_2_out, not_3_out, not_4_out, S0);
  and and_3 (A2, E, not_1_out, not_2_out, not_3_out, S1, not_5_out);
  and and_4 (A3, E, not_1_out, not_2_out, not_3_out, S1, S0);
  and and_5 (A4, E, not_1_out, not_2_out, S2, not_4_out, not_5_out);
  and and_6 (A5, E, not_1_out, not_2_out, S2, not_4_out, S0);
  and and_7 (A6, E, not_1_out, not_2_out, S2, S1, not_5_out);
  and and_8 (A7, E, not_1_out, not_2_out, S2, S1, S0);
  and and_9 (A8, E, not_1_out, S3, not_3_out, not_4_out, not_5_out);
  and and_10 (A9, E, not_1_out, S3, not_3_out, not_4_out, S0);
  and and_11 (A10, E, not_1_out, S3, not_3_out, S1, not_5_out);
  and and_12 (A11, E, not_1_out, S3, not_3_out, S1, S0);
  and and_13 (A12, E, not_1_out, S3, S2, not_4_out, not_5_out);
  and and_14 (A13, E, not_1_out, S3, S2, not_4_out, S0);
  and and_15 (A14, E, not_1_out, S3, S2, S1, not_5_out);
  and and_16 (A15, E, not_1_out, S3, S2, S1, S0);
  and and_17 (A16, E, S4, not_2_out, not_3_out, not_4_out, not_5_out);
  and and_18 (A17, E, S4, not_2_out, not_3_out, not_4_out, S0);
  and and_19 (A18, E, S4, not_2_out, not_3_out, S1, not_5_out);
  and and_20 (A19, E, S4, not_2_out, not_3_out, S1, S0);
  and and_21 (A20, E, S4, not_2_out, S2, not_4_out, not_5_out);
  and and_22 (A21, E, S4, not_2_out, S2, not_4_out, S0);
  and and_23 (A22, E, S4, not_2_out, S2, S1, not_5_out);
  and and_24 (A23, E, S4, not_2_out, S2, S1, S0);
  and and_25 (A24, E, S4, S3, not_3_out, not_4_out, not_5_out);
  and and_26 (A25, E, S4, S3, not_3_out, not_4_out, S0);
  and and_27 (A26, E, S4, S3, not_3_out, S1, not_5_out);
  and and_28 (A27, E, S4, S3, not_3_out, S1, S0);
  and and_29 (A28, E, S4, S3, S2, not_4_out, not_5_out);
  and and_30 (A29, E, S4, S3, S2, not_4_out, S0);
  and and_31 (A30, E, S4, S3, S2, S1, not_5_out);
  and and_32 (A31, E, S4, S3, S2, S1, S0);
endmodule
