// Logisim project Adder.circ as structural Verilog: 24 circuits, main circuit Full Adder
module Full_Adder (
  input  A,
  input  B,
  input  Cin,
  output S,
  output Cout
);

  wire and_1_out, and_2_out, xor_1_out;

  xor xor_1 (xor_1_out, A, B);
  xor xor_2 (S, xor_1_out, Cin);
  and and_1 (and_1_out, Cin, xor_1_out);
  and and_2 (and_2_out, B, A);
  or or_1 (Cout, and_1_out, and_2_out);
endmodule

module Adder___Subtractor (
  input  B7,
  input  A7,
  input  B6,
  input  A6,
  input  B5,
  input  A5,
  input  B4,
  input  A4,
  input  B3,
  input  A3,
  input  B2,
  input  A2,
  input  B1,
  input  A1,
  input  B0,
  input  A0,
  input  M,
  output Over_Flow,
  output C7,
  output C6,
  output C5,
  output C4,
  output C3,
  output C2,
  output C1,
  output C0
);

  wire full_adder_2_cout, full_adder_3_cout, full_adder_4_cout, full_adder_5_cout, full_adder_6_cout,
       full_adder_7_cout, full_adder_8_cout, xor_1_out, xor_2_out, xor_3_out, xor_4_out, xor_5_out,
       xor_6_out, xor_7_out, xor_8_out;

  xor xor_1 (xor_1_out, B7, M);
  xor xor_2 (xor_2_out, B6, M);
  Full_Adder full_adder_1 (.S(C7), .Cout(Over_Flow), .A(A7), .B(xor_1_out), .Cin(full_adder_2_cout));
  Full_Adder full_adder_2 (.S(C6), .Cout(full_adder_2_cout), .A(A6), .B(xor_2_out), .Cin(full_adder_3_cout));
  xor xor_3 (xor_3_out, B5, M);
  Full_Adder full_adder_3 (.S(C5), .Cout(full_adder_3_cout), .A(A5), .B(xor_3_out), .Cin(full_adder_4_cout));
  xor xor_4 (xor_4_out, B4, M);
  Full_Adder full_adder_4 (.S(C4), .Cout(full_adder_4_cout), .A(A4), .B(xor_4_out), .Cin(full_adder_5_cout));
  xor xor_5 (xor_5_out, B3, M);
  Full_Adder full_adder_5 (.S(C3), .Cout(full_adder_5_cout), .A(A3), .B(xor_5_out), .Cin(full_adder_6_cout));
  xor xor_6 (xor_6_out, B2, M);
  Full_Adder full_adder_6 (.S(C2), .Cout(full_adder_6_cout), .A(A2), .B(xor_6_out), .Cin(full_adder_7_cout));
  xor xor_7 (xor_7_out, B1, M);
  Full_Adder full_adder_7 (.S(C1), .Cout(full_adder_7_cout), .A(A1), .B(xor_7_out), .Cin(full_adder_8_cout));
  xor xor_8 (xor_8_out, B0, M);
  Full_Adder full_adder_8 (.S(C0), .Cout(full_adder_8_cout), .A(A0), .B(xor_8_out), .Cin(M));
endmodule

module Multiplier_8_Bit (
  input  A7,
  input  A6,
  input  A5,
  input  A4,
  input  A3,
  input  A2,
  input  A1,
  input  A0,
  input  B7,
  input  B6,
  input  B5,
  input  B4,
  input  B3,
  input  B2,
  input  B1,
  input  B0,
  output C15,
  output C14,
  output C13,
  output C12,
  output C11,
  output C10,
  output C9,
  output C8,
  output C7,
  output C6,
  output C5,
  output C4,
  output C3,
  output C2,
  output C1,
  output C0
);

  wire adder_subtractor_2_c1, adder_subtractor_2_c2, adder_subtractor_2_c3, adder_subtractor_2_c4,
       adder_subtractor_2_c5, adder_subtractor_2_c6, adder_subtractor_2_c7, adder_subtractor_2_over_flow,
       adder_subtractor_3_c1, adder_subtractor_3_c2, adder_subtractor_3_c3, adder_subtractor_3_c4,
       adder_subtractor_3_c5, adder_subtractor_3_c6, adder_subtractor_3_c7, adder_subtractor_3_over_flow,
       adder_subtractor_4_c1, adder_subtractor_4_c2, adder_subtractor_4_c3, adder_subtractor_4_c4,
       adder_subtractor_4_c5, adder_subtractor_4_c6, adder_subtractor_4_c7, adder_subtractor_4_over_flow,
       adder_subtractor_5_c1, adder_subtractor_5_c2, adder_subtractor_5_c3, adder_subtractor_5_c4,
       adder_subtractor_5_c5, adder_subtractor_5_c6, adder_subtractor_5_c7, adder_subtractor_5_over_flow,
       adder_subtractor_6_c1, adder_subtractor_6_c2, adder_subtractor_6_c3, adder_subtractor_6_c4,
       adder_subtractor_6_c5, adder_subtractor_6_c6, adder_subtractor_6_c7, adder_subtractor_6_over_flow,
       adder_subtractor_7_c1, adder_subtractor_7_c2, adder_subtractor_7_c3, adder_subtractor_7_c4,
       adder_subtractor_7_c5, adder_subtractor_7_c6, adder_subtractor_7_c7, adder_subtractor_7_over_flow,
       and_1_out, and_2_out, and_3_out, and_4_out, and_5_out, and_6_out, and_7_out, and_8_out, and_9_out,
       and_10_out, and_11_out, and_12_out, and_13_out, and_14_out, and_15_out, and_16_out, and_17_out,
       and_18_out, and_19_out, and_20_out, and_21_out, and_22_out, and_23_out, and_24_out, and_25_out,
       and_26_out, and_27_out, and_28_out, and_29_out, and_30_out, and_31_out, and_32_out, and_33_out,
       and_34_out, and_35_out, and_36_out, and_37_out, and_38_out, and_39_out, and_40_out, and_41_out,
       and_42_out, and_43_out, and_44_out, and_45_out, and_46_out, and_47_out, and_48_out, and_49_out,
       and_50_out, and_51_out, and_52_out, and_53_out, and_54_out, and_55_out, and_56_out, and_57_out,
       and_58_out, and_59_out, and_60_out, and_61_out, and_62_out, and_64_out;

  and and_1 (and_1_out, B7, A7);
  and and_2 (and_2_out, B6, A7);
  and and_3 (and_3_out, B5, A7);
  and and_4 (and_4_out, B3, A7);
  and and_5 (and_5_out, B4, A7);
  and and_6 (and_6_out, B7, A6);
  and and_7 (and_7_out, B6, A6);
  and and_8 (and_8_out, B2, A7);
  and and_9 (and_9_out, B1, A7);
  and and_10 (and_10_out, B0, A7);
  and and_11 (and_11_out, B4, A6);
  and and_12 (and_12_out, B3, A6);
  and and_13 (and_13_out, B5, A6);
  and and_14 (and_14_out, B6, A5);
  and and_15 (and_15_out, B7, A5);
  and and_16 (and_16_out, B2, A6);
  and and_17 (and_17_out, B1, A6);
  and and_18 (and_18_out, B5, A5);
  and and_19 (and_19_out, B4, A5);
  and and_20 (and_20_out, B0, A6);
  and and_21 (and_21_out, B7, A4);
  and and_22 (and_22_out, B3, A5);
  and and_23 (and_23_out, B1, A5);
  and and_24 (and_24_out, B2, A5);
  Adder___Subtractor adder_subtractor_1 (
    .M(1'b0), .B7(and_1_out), .A7(adder_subtractor_2_over_flow), .B6(and_2_out), .A6(adder_subtractor_2_c7),
    .B5(and_3_out), .A5(adder_subtractor_2_c6), .B4(and_5_out), .A4(adder_subtractor_2_c5), .B3(and_4_out),
    .A3(adder_subtractor_2_c4), .B2(and_8_out), .A2(adder_subtractor_2_c3), .B1(and_9_out),
    .A1(adder_subtractor_2_c2), .B0(and_10_out), .A0(adder_subtractor_2_c1), .Over_Flow(C15), .C7(C14),
    .C6(C13), .C5(C12), .C4(C11), .C3(C10), .C2(C9), .C1(C8), .C0(C7));
  and and_25 (and_25_out, B6, A4);
  and and_26 (and_26_out, B4, A4);
  and and_27 (and_27_out, B5, A4);
  and and_28 (and_28_out, B0, A5);
  and and_29 (and_29_out, B7, A3);
  and and_30 (and_30_out, B2, A4);
  and and_31 (and_31_out, B1, A4);
  and and_32 (and_32_out, B3, A4);
  Adder___Subtractor adder_subtractor_2 (
    .M(1'b0), .B7(and_6_out), .A7(adder_subtractor_3_over_flow), .B6(and_7_out), .A6(adder_subtractor_3_c7),
    .B5(and_13_out), .A5(adder_subtractor_3_c6), .B4(and_11_out), .A4(adder_subtractor_3_c5),
    .B3(and_12_out), .A3(adder_subtractor_3_c4), .B2(and_16_out), .A2(adder_subtractor_3_c3),
    .B1(and_17_out), .A1(adder_subtractor_3_c2), .B0(and_20_out), .A0(adder_subtractor_3_c1),
    .Over_Flow(adder_subtractor_2_over_flow), .C7(adder_subtractor_2_c7), .C6(adder_subtractor_2_c6),
    .C5(adder_subtractor_2_c5), .C4(adder_subtractor_2_c4), .C3(adder_subtractor_2_c3),
    .C2(adder_subtractor_2_c2), .C1(adder_subtractor_2_c1), .C0(C6));
  and and_33 (and_33_out, B5, A3);
  and and_34 (and_34_out, B4, A3);
  and and_35 (and_35_out, B6, A3);
  and and_36 (and_36_out, B0, A4);
  and and_37 (and_37_out, B7, A2);
  and and_38 (and_38_out, B3, A3);
  and and_39 (and_39_out, B2, A3);
  Adder___Subtractor adder_subtractor_3 (
    .M(1'b0), .B7(and_15_out), .A7(adder_subtractor_4_over_flow), .B6(and_14_out),
    .A6(adder_subtractor_4_c7), .B5(and_18_out), .A5(adder_subtractor_4_c6), .B4(and_19_out),
    .A4(adder_subtractor_4_c5), .B3(and_22_out), .A3(adder_subtractor_4_c4), .B2(and_24_out),
    .A2(adder_subtractor_4_c3), .B1(and_23_out), .A1(adder_subtractor_4_c2), .B0(and_28_out),
    .A0(adder_subtractor_4_c1), .Over_Flow(adder_subtractor_3_over_flow), .C7(adder_subtractor_3_c7),
    .C6(adder_subtractor_3_c6), .C5(adder_subtractor_3_c5), .C4(adder_subtractor_3_c4),
    .C3(adder_subtractor_3_c3), .C2(adder_subtractor_3_c2), .C1(adder_subtractor_3_c1), .C0(C5));
  and and_40 (and_40_out, B5, A2);
  and and_41 (and_41_out, B6, A2);
  and and_42 (and_42_out, B1, A3);
  and and_43 (and_43_out, B0, A3);
  and and_44 (and_44_out, B2, A2);
  and and_45 (and_45_out, B4, A2);
  and and_46 (and_46_out, B3, A2);
  and and_47 (and_47_out, B6, A1);
  and and_48 (and_48_out, B7, A1);
  and and_49 (and_49_out, B5, A1);
  and and_50 (and_50_out, B1, A2);
  and and_51 (and_51_out, B0, A2);
  Adder___Subtractor adder_subtractor_4 (
    .M(1'b0), .B7(and_21_out), .A7(adder_subtractor_5_over_flow), .B6(and_25_out),
    .A6(adder_subtractor_5_c7), .B5(and_27_out), .A5(adder_subtractor_5_c6), .B4(and_26_out),
    .A4(adder_subtractor_5_c5), .B3(and_32_out), .A3(adder_subtractor_5_c4), .B2(and_30_out),
    .A2(adder_subtractor_5_c3), .B1(and_31_out), .A1(adder_subtractor_5_c2), .B0(and_36_out),
    .A0(adder_subtractor_5_c1), .Over_Flow(adder_subtractor_4_over_flow), .C7(adder_subtractor_4_c7),
    .C6(adder_subtractor_4_c6), .C5(adder_subtractor_4_c5), .C4(adder_subtractor_4_c4),
    .C3(adder_subtractor_4_c3), .C2(adder_subtractor_4_c2), .C1(adder_subtractor_4_c1), .C0(C4));
  and and_52 (and_52_out, B3, A1);
  and and_53 (and_53_out, B2, A1);
  and and_54 (and_54_out, B4, A1);
  and and_55 (and_55_out, B1, A1);
  and and_56 (and_56_out, B0, A1);
  Adder___Subtractor adder_subtractor_5 (
    .M(1'b0), .B7(and_29_out), .A7(adder_subtractor_6_over_flow), .B6(and_35_out),
    .A6(adder_subtractor_6_c7), .B5(and_33_out), .A5(adder_subtractor_6_c6), .B4(and_34_out),
    .A4(adder_subtractor_6_c5), .B3(and_38_out), .A3(adder_subtractor_6_c4), .B2(and_39_out),
    .A2(adder_subtractor_6_c3), .B1(and_42_out), .A1(adder_subtractor_6_c2), .B0(and_43_out),
    .A0(adder_subtractor_6_c1), .Over_Flow(adder_subtractor_5_over_flow), .C7(adder_subtractor_5_c7),
    .C6(adder_subtractor_5_c6), .C5(adder_subtractor_5_c5), .C4(adder_subtractor_5_c4),
    .C3(adder_subtractor_5_c3), .C2(adder_subtractor_5_c2), .C1(adder_subtractor_5_c1), .C0(C3));
  and and_57 (and_57_out, B7, A0);
  and and_58 (and_58_out, B6, A0);
  and and_59 (and_59_out, B5, A0);
  Adder___Subtractor adder_subtractor_6 (
    .M(1'b0), .B7(and_37_out), .A7(adder_subtractor_7_over_flow), .B6(and_41_out),
    .A6(adder_subtractor_7_c7), .B5(and_40_out), .A5(adder_subtractor_7_c6), .B4(and_45_out),
    .A4(adder_subtractor_7_c5), .B3(and_46_out), .A3(adder_subtractor_7_c4), .B2(and_44_out),
    .A2(adder_subtractor_7_c3), .B1(and_50_out), .A1(adder_subtractor_7_c2), .B0(and_51_out),
    .A0(adder_subtractor_7_c1), .Over_Flow(adder_subtractor_6_over_flow), .C7(adder_subtractor_6_c7),
    .C6(adder_subtractor_6_c6), .C5(adder_subtractor_6_c5), .C4(adder_subtractor_6_c4),
    .C3(adder_subtractor_6_c3), .C2(adder_subtractor_6_c2), .C1(adder_subtractor_6_c1), .C0(C2));
  and and_60 (and_60_out, B4, A0);
  and and_61 (and_61_out, B2, A0);
  and and_62 (and_62_out, B3, A0);
  and and_63 (C0, B0, A0);
  and and_64 (and_64_out, B1, A0);
  Adder___Subtractor adder_subtractor_7 (
    .M(1'b0), .B7(and_48_out), .A7(1'b0), .B6(and_47_out), .A6(and_57_out), .B5(and_49_out), .A5(and_58_out),
    .B4(and_54_out), .A4(and_59_out), .B3(and_52_out), .A3(and_60_out), .B2(and_53_out), .A2(and_62_out),
    .B1(and_55_out), .A1(and_61_out), .B0(and_56_out), .A0(and_64_out),
    .Over_Flow(adder_subtractor_7_over_flow), .C7(adder_subtractor_7_c7), .C6(adder_subtractor_7_c6),
    .C5(adder_subtractor_7_c5), .C4(adder_subtractor_7_c4), .C3(adder_subtractor_7_c3),
    .C2(adder_subtractor_7_c2), .C1(adder_subtractor_7_c1), .C0(C1));
endmodule

module Adder_by_1 (
  input  A7,
  input  A6,
  input  A5,
  input  A4,
  input  A3,
  input  A2,
  input  A1,
  input  A0,
  output Over_Flow,
  output B7,
  output B6,
  output B5,
  output B4,
  output B3,
  output B2,
  output B1,
  output B0
);

  Adder___Subtractor adder_subtractor_1 (
    .M(1'b0), .B7(1'b0), .A7(A7), .B6(1'b0), .A6(A6), .B5(1'b0), .A5(A5), .B4(1'b0), .A4(A4), .B3(1'b0),
    .A3(A3), .B2(1'b0), .A2(A2), .B1(1'b0), .A1(A1), .B0(1'b1), .A0(A0), .Over_Flow(Over_Flow), .C7(B7),
    .C6(B6), .C5(B5), .C4(B4), .C3(B3), .C2(B2), .C1(B1), .C0(B0));
endmodule

module Subtractor_by_1 (
  input  A7,
  input  A6,
  input  A5,
  input  A4,
  input  A3,
  input  A2,
  input  A1,
  input  A0,
  output Over_Flow,
  output B7,
  output B6,
  output B5,
  output B4,
  output B3,
  output B2,
  output B1,
  output B0
);

  Adder___Subtractor adder_subtractor_1 (
    .M(1'b1), .B7(1'b0), .A7(A7), .B6(1'b0), .A6(A6), .B5(1'b0), .A5(A5), .B4(1'b0), .A4(A4), .B3(1'b0),
    .A3(A3), .B2(1'b0), .A2(A2), .B1(1'b0), .A1(A1), .B0(1'b1), .A0(A0), .Over_Flow(Over_Flow), .C7(B7),
    .C6(B6), .C5(B5), .C4(B4), .C3(B3), .C2(B2), .C1(B1), .C0(B0));
endmodule

module And (
  input  A0,
  input  A1,
  input  A2,
  input  A3,
  input  A4,
  input  A5,
  input  A6,
  input  A7,
  input  B0,
  input  B1,
  input  B2,
  input  B3,
  input  B4,
  input  B5,
  input  B6,
  input  B7,
  input  E,
  output C0,
  output C1,
  output C2,
  output C3,
  output C4,
  output C5,
  output C6,
  output C7
);

  wire and_1_out, and_3_out, and_5_out, and_7_out, and_9_out, and_11_out, and_13_out, and_15_out;

  and and_1 (and_1_out, A0, B0);
  and and_2 (C0, and_1_out, E);
  and and_3 (and_3_out, A1, B1);
  and and_4 (C1, and_3_out, E);
  and and_5 (and_5_out, A2, B2);
  and and_6 (C2, and_5_out, E);
  and and_7 (and_7_out, A3, B3);
  and and_8 (C3, and_7_out, E);
  and and_9 (and_9_out, A4, B4);
  and and_10 (C4, and_9_out, E);
  and and_11 (and_11_out, A5, B5);
  and and_12 (C5, and_11_out, E);
  and and_13 (and_13_out, A6, B6);
  and and_14 (C6, and_13_out, E);
  and and_15 (and_15_out, A7, B7);
  and and_16 (C7, and_15_out, E);
endmodule

module OR (
  input  A0,
  input  A1,
  input  A2,
  input  A3,
  input  A4,
  input  A5,
  input  A6,
  input  A7,
  input  B0,
  input  B1,
  input  B2,
  input  B3,
  input  B4,
  input  B5,
  input  B6,
  input  B7,
  input  E,
  output C0,
  output C1,
  output C2,
  output C3,
  output C4,
  output C5,
  output C6,
  output C7
);

  wire or_1_out, or_2_out, or_3_out, or_4_out, or_5_out, or_6_out, or_7_out, or_8_out;

  or or_1 (or_1_out, A0, B0);
  and and_1 (C0, or_1_out, E);
  or or_2 (or_2_out, A1, B1);
  and and_2 (C1, or_2_out, E);
  or or_3 (or_3_out, A2, B2);
  and and_3 (C2, or_3_out, E);
  or or_4 (or_4_out, A3, B3);
  and and_4 (C3, or_4_out, E);
  or or_5 (or_5_out, A4, B4);
  and and_5 (C4, or_5_out, E);
  or or_6 (or_6_out, A5, B5);
  and and_6 (C5, or_6_out, E);
  or or_7 (or_7_out, A6, B6);
  and and_7 (C6, or_7_out, E);
  or or_8 (or_8_out, A7, B7);
  and and_8 (C7, or_8_out, E);
endmodule

module XOR (
  input  A0,
  input  A1,
  input  A2,
  input  A3,
  input  A4,
  input  A5,
  input  A6,
  input  A7,
  input  B0,
  input  B1,
  input  B2,
  input  B3,
  input  B4,
  input  B5,
  input  B6,
  input  B7,
  input  E,
  output C0,
  output C1,
  output C2,
  output C3,
  output C4,
  output C5,
  output C6,
  output C7
);

  wire xor_1_out, xor_2_out, xor_3_out, xor_4_out, xor_5_out, xor_6_out, xor_7_out, xor_8_out;

  xor xor_1 (xor_1_out, A0, B0);
  xor xor_2 (xor_2_out, A1, B1);
  xor xor_3 (xor_3_out, A2, B2);
  xor xor_4 (xor_4_out, A3, B3);
  xor xor_5 (xor_5_out, A4, B4);
  xor xor_6 (xor_6_out, A5, B5);
  xor xor_7 (xor_7_out, A6, B6);
  xor xor_8 (xor_8_out, A7, B7);
  and and_1 (C0, xor_1_out, E);
  and and_2 (C1, xor_2_out, E);
  and and_3 (C2, xor_3_out, E);
  and and_4 (C3, xor_4_out, E);
  and and_5 (C4, xor_5_out, E);
  and and_6 (C5, xor_6_out, E);
  and and_7 (C6, xor_7_out, E);
  and and_8 (C7, xor_8_out, E);
endmodule

module NOT (
  input  A0,
  input  A1,
  input  A2,
  input  A3,
  input  A4,
  input  A5,
  input  A6,
  input  A7,
  input  E,
  output C0,
  output C1,
  output C2,
  output C3,
  output C4,
  output C5,
  output C6,
  output C7
);

  wire not_1_out, not_2_out, not_3_out, not_4_out, not_5_out, not_6_out, not_7_out, not_8_out;

  not not_1 (not_1_out, A0);
  not not_2 (not_2_out, A1);
  not not_3 (not_3_out, A2);
  not not_4 (not_4_out, A3);
  not not_5 (not_5_out, A4);
  not not_6 (not_6_out, A5);
  not not_7 (not_7_out, A6);
  not not_8 (not_8_out, A7);
  and and_1 (C0, not_1_out, E);
  and and_2 (C1, not_2_out, E);
  and and_3 (C2, not_3_out, E);
  and and_4 (C3, not_4_out, E);
  and and_5 (C4, not_5_out, E);
  and and_6 (C5, not_6_out, E);
  and and_7 (C6, not_7_out, E);
  and and_8 (C7, not_8_out, E);
endmodule

module SLA (
  input  Rotate,
  input  E,
  input  A7,
  input  A6,
  input  A5,
  input  A4,
  input  A3,
  input  A2,
  input  A1,
  input  A0,
  output B7,
  output B6,
  output B5,
  output B4,
  output B3,
  output B2,
  output B1,
  output B0
);

  wire and_9_out;

  and and_1 (B7, E, A6);
  and and_2 (B5, E, A4);
  and and_3 (B4, E, A3);
  and and_4 (B6, E, A5);
  and and_5 (B3, E, A2);
  and and_6 (B1, E, A0);
  and and_7 (B2, E, A1);
  and and_8 (B0, E, and_9_out);
  and and_9 (and_9_out, Rotate, A7);
endmodule

module Test (
  input  in_1,
  input  in_2,
  input  in_3,
  input  in_4,
  input  in_5,
  input  in_6,
  input  in_7,
  input  in_8,
  input  in_9,
  input  in_10,
  input  in_11,
  input  in_12,
  input  in_13,
  input  in_14,
  input  in_15,
  input  in_16,
  input  B7,
  input  B6,
  input  B5,
  input  B4,
  input  B3,
  input  B2,
  input  B1,
  input  B0,
  input  A7,
  input  A6,
  input  A5,
  input  A4,
  input  A3,
  input  A2,
  input  A1,
  input  A0,
  input  S0,
  input  S1,
  input  E,
  input  S2,
  input  in_37,
  input  S3,
  input  S4,
  output out_40,
  output out_41,
  output out_42,
  output out_43,
  output out_44,
  output out_45,
  output out_46,
  output out_47,
  output out_48,
  output out_49,
  output out_50,
  output out_51,
  output out_52,
  output out_53,
  output out_54,
  output out_55,
  output Over_Flow,
  output out_57,
  output out_58,
  output out_59,
  output out_60,
  output out_61,
  output out_62,
  output out_63,
  output out_64
);

  ALU alu_1 (
    .A0(A0), .A1(A1), .A2(A2), .A3(A3), .A4(A4), .A5(A5), .A6(A6), .A7(A7), .B0(B0), .B1(B1), .B2(B2),
    .B3(B3), .B4(B4), .B5(B5), .B6(B6), .B7(B7), .Rotate_Shift(in_37), .E(E), .Over_Flow(Over_Flow), .S4(S4),
    .S3(S3), .S2(S2), .S1(S1), .S0(S0), .C0(out_64), .C1(out_63), .C2(out_62), .C3(out_61), .C4(out_60),
    .C5(out_59), .C6(out_58), .C7(out_57));
  Multiplier_8_Bit multiplier_8_bit_1 (
    .A0(in_8), .A1(in_7), .A2(in_6), .A3(in_5), .A4(in_4), .A5(in_3), .A6(in_2), .A7(in_1), .B7(in_9),
    .B6(in_10), .B5(in_11), .B4(in_12), .B3(in_13), .B2(in_14), .B1(in_15), .B0(in_16), .C15(out_40),
    .C14(out_41), .C13(out_42), .C12(out_43), .C11(out_44), .C10(out_45), .C9(out_46), .C8(out_47),
    .C7(out_48), .C6(out_49), .C5(out_50), .C4(out_51), .C3(out_52), .C2(out_53), .C1(out_54), .C0(out_55));
endmodule

module Multiplier_8_Bit_New (
  input  in_1,
  input  in_2,
  input  in_3,
  input  in_4,
  input  in_5,
  input  in_6,
  input  in_7,
  input  in_8,
  input  in_9,
  input  in_10,
  input  in_11,
  input  in_12,
  input  in_13,
  input  in_14,
  input  in_15,
  input  in_16,
  output out_17,
  output out_18,
  output out_19,
  output out_20,
  output out_21,
  output out_22,
  output out_23,
  output out_24,
  output out_25,
  output out_26,
  output out_27,
  output out_28,
  output out_29,
  output out_30,
  output out_31,
  output out_32
);

  wire and_1_out, and_2_out, and_3_out, and_4_out, and_5_out, and_6_out, and_7_out, and_8_out, and_9_out,
       and_10_out, and_11_out, and_12_out, and_13_out, and_14_out, and_15_out, and_16_out, and_17_out,
       and_18_out, and_19_out, and_20_out, and_21_out, and_22_out, and_23_out, and_24_out, and_25_out,
       and_26_out, and_27_out, and_28_out, and_29_out, and_30_out, and_31_out, and_32_out, and_33_out,
       and_34_out, and_35_out, and_36_out, and_37_out, and_38_out, and_39_out, and_40_out, and_41_out,
       and_42_out, and_43_out, and_44_out, and_45_out, and_46_out, and_47_out, and_48_out, and_49_out,
       and_50_out, and_51_out, and_52_out, and_53_out, and_54_out, and_55_out, and_56_out, and_57_out,
       and_58_out, and_59_out, and_60_out, and_61_out, and_62_out, and_63_out, and_65_out, and_66_out,
       full_adder_new_2_cout, full_adder_new_2_s, full_adder_new_3_cout, full_adder_new_4_cout,
       full_adder_new_4_s, full_adder_new_5_cout, full_adder_new_5_s, full_adder_new_6_cout,
       full_adder_new_7_cout, full_adder_new_7_s, full_adder_new_8_cout, full_adder_new_8_s,
       full_adder_new_9_cout, full_adder_new_10_cout, full_adder_new_10_s, full_adder_new_11_cout,
       full_adder_new_11_s, full_adder_new_12_cout, full_adder_new_12_s, full_adder_new_13_cout,
       full_adder_new_14_cout, full_adder_new_14_s, full_adder_new_15_cout, full_adder_new_15_s,
       full_adder_new_16_cout, full_adder_new_16_s, full_adder_new_17_cout, full_adder_new_17_s,
       full_adder_new_18_cout, full_adder_new_19_cout, full_adder_new_19_s, full_adder_new_20_cout,
       full_adder_new_20_s, full_adder_new_21_cout, full_adder_new_21_s, full_adder_new_22_cout,
       full_adder_new_22_s, full_adder_new_23_cout, full_adder_new_23_s, full_adder_new_24_cout,
       full_adder_new_25_cout, full_adder_new_25_s, full_adder_new_26_cout, full_adder_new_26_s,
       full_adder_new_27_cout, full_adder_new_27_s, full_adder_new_28_cout, full_adder_new_28_s,
       full_adder_new_29_cout, full_adder_new_29_s, full_adder_new_30_cout, full_adder_new_30_s,
       full_adder_new_31_cout, full_adder_new_32_cout, full_adder_new_32_s, full_adder_new_33_cout,
       full_adder_new_33_s, full_adder_new_34_cout, full_adder_new_34_s, full_adder_new_35_cout,
       full_adder_new_35_s, full_adder_new_36_cout, full_adder_new_36_s, full_adder_new_37_cout,
       full_adder_new_38_cout, full_adder_new_38_s, full_adder_new_39_cout, full_adder_new_39_s,
       full_adder_new_40_cout, full_adder_new_40_s, full_adder_new_41_cout, full_adder_new_41_s,
       full_adder_new_42_cout, full_adder_new_43_cout, full_adder_new_43_s, full_adder_new_44_cout,
       full_adder_new_44_s, full_adder_new_45_cout, full_adder_new_45_s, full_adder_new_46_cout,
       full_adder_new_46_s, full_adder_new_47_cout, full_adder_new_47_s, full_adder_new_48_cout,
       full_adder_new_48_s, full_adder_new_49_cout, full_adder_new_49_s, full_adder_new_50_cout,
       full_adder_new_51_cout, full_adder_new_51_s, full_adder_new_52_cout, full_adder_new_52_s,
       full_adder_new_53_cout, full_adder_new_54_cout, full_adder_new_54_s, full_adder_new_55_cout,
       full_adder_new_56_cout, undriven, undriven_2, undriven_3, undriven_4;

  and and_1 (and_1_out, in_1, in_9);
  Full_Adder_New full_adder_new_1 (
    .A(full_adder_new_2_cout), .B(and_1_out), .Cin(full_adder_new_3_cout), .S(out_18), .Cout(out_17));
  and and_2 (and_2_out, in_2, in_9);
  Full_Adder_New full_adder_new_2 (
    .A(full_adder_new_4_cout), .B(and_2_out), .Cin(full_adder_new_5_cout), .S(full_adder_new_2_s),
    .Cout(full_adder_new_2_cout));
  and and_3 (and_3_out, in_1, in_10);
  Full_Adder_New full_adder_new_3 (
    .A(full_adder_new_2_s), .B(and_3_out), .Cin(full_adder_new_6_cout), .S(out_19),
    .Cout(full_adder_new_3_cout));
  and and_4 (and_4_out, in_3, in_9);
  Full_Adder_New full_adder_new_4 (
    .A(full_adder_new_10_cout), .B(and_4_out), .Cin(full_adder_new_7_cout), .S(full_adder_new_4_s),
    .Cout(full_adder_new_4_cout));
  and and_5 (and_5_out, in_2, in_10);
  Full_Adder_New full_adder_new_5 (
    .A(full_adder_new_4_s), .B(and_5_out), .Cin(full_adder_new_8_cout), .S(full_adder_new_5_s),
    .Cout(full_adder_new_5_cout));
  and and_6 (and_6_out, in_1, in_11);
  Full_Adder_New full_adder_new_6 (
    .A(full_adder_new_5_s), .B(and_6_out), .Cin(full_adder_new_9_cout), .S(out_20),
    .Cout(full_adder_new_6_cout));
  and and_7 (and_7_out, in_4, in_9);
  and and_8 (and_8_out, in_3, in_10);
  Full_Adder_New full_adder_new_7 (
    .A(full_adder_new_10_s), .B(and_8_out), .Cin(full_adder_new_11_cout), .S(full_adder_new_7_s),
    .Cout(full_adder_new_7_cout));
  and and_9 (and_9_out, in_2, in_11);
  Full_Adder_New full_adder_new_8 (
    .A(full_adder_new_7_s), .B(and_9_out), .Cin(full_adder_new_12_cout), .S(full_adder_new_8_s),
    .Cout(full_adder_new_8_cout));
  and and_10 (and_10_out, in_1, in_12);
  Full_Adder_New full_adder_new_9 (
    .A(full_adder_new_8_s), .B(and_10_out), .Cin(full_adder_new_13_cout), .S(out_21),
    .Cout(full_adder_new_9_cout));
  and and_11 (and_11_out, in_4, in_10);
  Full_Adder_New full_adder_new_10 (
    .A(full_adder_new_14_cout), .B(and_7_out), .Cin(full_adder_new_15_cout), .S(full_adder_new_10_s),
    .Cout(full_adder_new_10_cout));
  and and_12 (and_12_out, in_3, in_11);
  Full_Adder_New full_adder_new_11 (
    .A(full_adder_new_15_s), .B(and_12_out), .Cin(full_adder_new_16_cout), .S(full_adder_new_11_s),
    .Cout(full_adder_new_11_cout));
  and and_13 (and_13_out, in_2, in_12);
  Full_Adder_New full_adder_new_12 (
    .A(full_adder_new_11_s), .B(and_13_out), .Cin(full_adder_new_17_cout), .S(full_adder_new_12_s),
    .Cout(full_adder_new_12_cout));
  and and_14 (and_14_out, in_1, in_13);
  Full_Adder_New full_adder_new_13 (
    .A(full_adder_new_12_s), .B(and_14_out), .Cin(full_adder_new_18_cout), .S(out_22),
    .Cout(full_adder_new_13_cout));
  and and_15 (and_15_out, in_5, in_9);
  Full_Adder_New full_adder_new_14 (
    .A(full_adder_new_19_cout), .B(and_15_out), .Cin(full_adder_new_20_cout), .S(full_adder_new_14_s),
    .Cout(full_adder_new_14_cout));
  and and_16 (and_16_out, in_4, in_11);
  Full_Adder_New full_adder_new_15 (
    .A(full_adder_new_14_s), .B(and_11_out), .Cin(full_adder_new_21_cout), .S(full_adder_new_15_s),
    .Cout(full_adder_new_15_cout));
  and and_17 (and_17_out, in_3, in_12);
  Full_Adder_New full_adder_new_16 (
    .A(full_adder_new_21_s), .B(and_17_out), .Cin(full_adder_new_22_cout), .S(full_adder_new_16_s),
    .Cout(full_adder_new_16_cout));
  and and_18 (and_18_out, in_2, in_13);
  Full_Adder_New full_adder_new_17 (
    .A(full_adder_new_16_s), .B(and_18_out), .Cin(full_adder_new_23_cout), .S(full_adder_new_17_s),
    .Cout(full_adder_new_17_cout));
  and and_19 (and_19_out, in_1, in_14);
  Full_Adder_New full_adder_new_18 (
    .A(full_adder_new_17_s), .B(and_19_out), .Cin(full_adder_new_24_cout), .S(out_23),
    .Cout(full_adder_new_18_cout));
  and and_20 (and_20_out, in_6, in_9);
  Full_Adder_New full_adder_new_19 (
    .A(full_adder_new_25_cout), .B(and_20_out), .Cin(full_adder_new_26_cout), .S(full_adder_new_19_s),
    .Cout(full_adder_new_19_cout));
  and and_21 (and_21_out, in_5, in_10);
  Full_Adder_New full_adder_new_20 (
    .A(full_adder_new_19_s), .B(and_21_out), .Cin(full_adder_new_27_cout), .S(full_adder_new_20_s),
    .Cout(full_adder_new_20_cout));
  and and_22 (and_22_out, in_4, in_12);
  Full_Adder_New full_adder_new_21 (
    .A(full_adder_new_20_s), .B(and_16_out), .Cin(full_adder_new_28_cout), .S(full_adder_new_21_s),
    .Cout(full_adder_new_21_cout));
  and and_23 (and_23_out, in_3, in_13);
  Full_Adder_New full_adder_new_22 (
    .A(full_adder_new_28_s), .B(and_23_out), .Cin(full_adder_new_29_cout), .S(full_adder_new_22_s),
    .Cout(full_adder_new_22_cout));
  and and_24 (and_24_out, in_2, in_14);
  Full_Adder_New full_adder_new_23 (
    .A(full_adder_new_22_s), .B(and_24_out), .Cin(full_adder_new_30_cout), .S(full_adder_new_23_s),
    .Cout(full_adder_new_23_cout));
  and and_25 (and_25_out, in_1, in_15);
  Full_Adder_New full_adder_new_24 (
    .A(full_adder_new_23_s), .B(and_25_out), .Cin(full_adder_new_31_cout), .S(out_24),
    .Cout(full_adder_new_24_cout));
  and and_26 (and_26_out, in_7, in_9);
  Full_Adder_New full_adder_new_25 (
    .A(1'b0), .B(and_26_out), .Cin(full_adder_new_32_cout), .S(full_adder_new_25_s),
    .Cout(full_adder_new_25_cout));
  and and_27 (and_27_out, in_6, in_10);
  Full_Adder_New full_adder_new_26 (
    .A(full_adder_new_25_s), .B(and_27_out), .Cin(full_adder_new_33_cout), .S(full_adder_new_26_s),
    .Cout(full_adder_new_26_cout));
  and and_28 (and_28_out, in_5, in_11);
  Full_Adder_New full_adder_new_27 (
    .A(full_adder_new_26_s), .B(and_28_out), .Cin(full_adder_new_34_cout), .S(full_adder_new_27_s),
    .Cout(full_adder_new_27_cout));
  and and_29 (and_29_out, in_4, in_13);
  Full_Adder_New full_adder_new_28 (
    .A(full_adder_new_27_s), .B(and_22_out), .Cin(full_adder_new_35_cout), .S(full_adder_new_28_s),
    .Cout(full_adder_new_28_cout));
  and and_30 (and_30_out, in_3, in_14);
  Full_Adder_New full_adder_new_29 (
    .A(full_adder_new_35_s), .B(and_30_out), .Cin(full_adder_new_36_cout), .S(full_adder_new_29_s),
    .Cout(full_adder_new_29_cout));
  and and_31 (and_31_out, in_2, in_15);
  Full_Adder_New full_adder_new_30 (
    .A(full_adder_new_29_s), .B(and_31_out), .Cin(full_adder_new_37_cout), .S(full_adder_new_30_s),
    .Cout(full_adder_new_30_cout));
  and and_32 (and_32_out, in_1, in_16);
  Full_Adder_New full_adder_new_31 (
    .A(full_adder_new_30_s), .B(and_32_out), .Cin(1'b0), .S(out_25), .Cout(full_adder_new_31_cout));
  and and_33 (and_33_out, in_7, in_10);
  Full_Adder_New full_adder_new_32 (
    .A(and_39_out), .B(and_33_out), .Cin(full_adder_new_38_cout), .S(full_adder_new_32_s),
    .Cout(full_adder_new_32_cout));
  and and_34 (and_34_out, in_6, in_11);
  Full_Adder_New full_adder_new_33 (
    .A(full_adder_new_32_s), .B(and_34_out), .Cin(full_adder_new_39_cout), .S(full_adder_new_33_s),
    .Cout(full_adder_new_33_cout));
  and and_35 (and_35_out, in_5, in_12);
  Full_Adder_New full_adder_new_34 (
    .A(full_adder_new_33_s), .B(and_35_out), .Cin(full_adder_new_40_cout), .S(full_adder_new_34_s),
    .Cout(full_adder_new_34_cout));
  and and_36 (and_36_out, in_4, in_14);
  Full_Adder_New full_adder_new_35 (
    .A(full_adder_new_34_s), .B(and_29_out), .Cin(full_adder_new_41_cout), .S(full_adder_new_35_s),
    .Cout(full_adder_new_35_cout));
  and and_37 (and_37_out, in_3, in_15);
  Full_Adder_New full_adder_new_36 (
    .A(full_adder_new_41_s), .B(and_37_out), .Cin(full_adder_new_42_cout), .S(full_adder_new_36_s),
    .Cout(full_adder_new_36_cout));
  and and_38 (and_38_out, in_2, in_16);
  Full_Adder_New full_adder_new_37 (
    .A(full_adder_new_36_s), .B(and_38_out), .Cin(1'b0), .S(out_26), .Cout(full_adder_new_37_cout));
  and and_39 (and_39_out, in_8, in_9);
  and and_40 (and_40_out, in_7, in_11);
  Full_Adder_New full_adder_new_38 (
    .A(and_45_out), .B(and_40_out), .Cin(full_adder_new_43_cout), .S(full_adder_new_38_s),
    .Cout(full_adder_new_38_cout));
  and and_41 (and_41_out, in_6, in_12);
  Full_Adder_New full_adder_new_39 (
    .A(full_adder_new_38_s), .B(and_41_out), .Cin(full_adder_new_44_cout), .S(full_adder_new_39_s),
    .Cout(full_adder_new_39_cout));
  and and_42 (and_42_out, in_5, in_13);
  Full_Adder_New full_adder_new_40 (
    .A(full_adder_new_39_s), .B(and_42_out), .Cin(full_adder_new_45_cout), .S(full_adder_new_40_s),
    .Cout(full_adder_new_40_cout));
  and and_43 (and_43_out, in_4, in_15);
  Full_Adder_New full_adder_new_41 (
    .A(full_adder_new_40_s), .B(and_36_out), .Cin(full_adder_new_46_cout), .S(full_adder_new_41_s),
    .Cout(full_adder_new_41_cout));
  and and_44 (and_44_out, in_3, in_16);
  Full_Adder_New full_adder_new_42 (
    .A(full_adder_new_46_s), .B(and_44_out), .Cin(1'b0), .S(out_27), .Cout(full_adder_new_42_cout));
  and and_45 (and_45_out, in_8, in_10);
  and and_46 (and_46_out, in_7, in_12);
  Full_Adder_New full_adder_new_43 (
    .A(and_50_out), .B(and_46_out), .Cin(full_adder_new_47_cout), .S(full_adder_new_43_s),
    .Cout(full_adder_new_43_cout));
  and and_47 (and_47_out, in_6, in_13);
  Full_Adder_New full_adder_new_44 (
    .A(full_adder_new_43_s), .B(and_47_out), .Cin(full_adder_new_48_cout), .S(full_adder_new_44_s),
    .Cout(full_adder_new_44_cout));
  and and_48 (and_48_out, in_5, in_14);
  Full_Adder_New full_adder_new_45 (
    .A(full_adder_new_44_s), .B(and_48_out), .Cin(full_adder_new_49_cout), .S(full_adder_new_45_s),
    .Cout(full_adder_new_45_cout));
  and and_49 (and_49_out, in_4, in_16);
  Full_Adder_New full_adder_new_46 (
    .A(full_adder_new_45_s), .B(and_43_out), .Cin(full_adder_new_50_cout), .S(full_adder_new_46_s),
    .Cout(full_adder_new_46_cout));
  and and_50 (and_50_out, in_8, in_11);
  and and_51 (and_51_out, in_7, in_13);
  Full_Adder_New full_adder_new_47 (
    .A(and_54_out), .B(and_51_out), .Cin(full_adder_new_51_cout), .S(full_adder_new_47_s),
    .Cout(full_adder_new_47_cout));
  and and_52 (and_52_out, in_6, in_14);
  Full_Adder_New full_adder_new_48 (
    .A(full_adder_new_47_s), .B(and_52_out), .Cin(full_adder_new_52_cout), .S(full_adder_new_48_s),
    .Cout(full_adder_new_48_cout));
  and and_53 (and_53_out, in_5, in_15);
  Full_Adder_New full_adder_new_49 (
    .A(full_adder_new_48_s), .B(and_53_out), .Cin(full_adder_new_53_cout), .S(full_adder_new_49_s),
    .Cout(full_adder_new_49_cout));
  Full_Adder_New full_adder_new_50 (
    .A(full_adder_new_49_s), .B(and_49_out), .Cin(1'b0), .S(out_28), .Cout(full_adder_new_50_cout));
  and and_54 (and_54_out, in_8, in_12);
  and and_55 (and_55_out, in_7, in_14);
  Full_Adder_New full_adder_new_51 (
    .A(and_58_out), .B(and_55_out), .Cin(full_adder_new_54_cout), .S(full_adder_new_51_s),
    .Cout(full_adder_new_51_cout));
  and and_56 (and_56_out, in_6, in_15);
  Full_Adder_New full_adder_new_52 (
    .A(full_adder_new_51_s), .B(and_56_out), .Cin(full_adder_new_55_cout), .S(full_adder_new_52_s),
    .Cout(full_adder_new_52_cout));
  and and_57 (and_57_out, in_5, in_16);
  Full_Adder_New full_adder_new_53 (
    .A(full_adder_new_52_s), .B(and_57_out), .Cin(1'b0), .S(out_29), .Cout(full_adder_new_53_cout));
  and and_58 (and_58_out, in_8, in_13);
  and and_59 (and_59_out, in_7, in_15);
  Full_Adder_New full_adder_new_54 (
    .A(and_61_out), .B(and_59_out), .Cin(full_adder_new_56_cout), .S(full_adder_new_54_s),
    .Cout(full_adder_new_54_cout));
  and and_60 (and_60_out, in_6, in_16);
  Full_Adder_New full_adder_new_55 (
    .A(full_adder_new_54_s), .B(and_60_out), .Cin(1'b0), .S(out_30), .Cout(full_adder_new_55_cout));
  and and_61 (and_61_out, in_8, in_14);
  and and_62 (and_62_out, in_7, in_16);
  Full_Adder_New full_adder_new_56 (
    .A(and_63_out), .B(and_62_out), .Cin(1'b0), .S(out_31), .Cout(full_adder_new_56_cout));
  and and_63 (and_63_out, in_8, in_15);
  and and_64 (out_32, in_8, in_16);
  and and_65 (and_65_out, undriven_3, undriven_4);
  and and_66 (and_66_out, undriven, undriven_2);
  Full_Adder_New full_adder_new_57 (.A(and_65_out), .B(and_66_out));  // open: Cin, S, Cout
endmodule

module Full_Adder_New (
  input  A,
  input  B,
  input  Cin,
  output S,
  output Cout
);

  wire and_1_out, and_2_out, xor_1_out;

  xor xor_1 (xor_1_out, A, B);
  xor xor_2 (S, xor_1_out, Cin);
  and and_1 (and_1_out, Cin, xor_1_out);
  and and_2 (and_2_out, B, A);
  or or_1 (Cout, and_1_out, and_2_out);
endmodule

module ALU (
  input  A0,
  input  A1,
  input  A2,
  input  A3,
  input  A4,
  input  A5,
  input  A6,
  input  A7,
  input  B0,
  input  B1,
  input  B2,
  input  B3,
  input  B4,
  input  B5,
  input  B6,
  input  B7,
  input  E,
  input  Rotate_Shift,
  input  S4,
  input  S3,
  input  S2,
  input  S1,
  input  S0,
  output Over_Flow,
  output C0,
  output C1,
  output C2,
  output C3,
  output C4,
  output C5,
  output C6,
  output C7
);

  wire adder_by_1_e_1_b0, adder_by_1_e_1_b1, adder_by_1_e_1_b2, adder_by_1_e_1_b3, adder_by_1_e_1_b4,
       adder_by_1_e_1_b5, adder_by_1_e_1_b6, adder_by_1_e_1_b7, adder_by_1_e_1_over_flow, adder_e_1_c0,
       adder_e_1_c1, adder_e_1_c2, adder_e_1_c3, adder_e_1_c4, adder_e_1_c5, adder_e_1_c6, adder_e_1_c7,
       adder_e_1_over_flow, and_1_c0, and_1_c1, and_1_c2, and_1_c3, and_1_c4, and_1_c5, and_1_c6, and_1_c7,
       demux_1_32_1_a0, demux_1_32_1_a1, demux_1_32_1_a2, demux_1_32_1_a3, demux_1_32_1_a4, demux_1_32_1_a5,
       demux_1_32_1_a6, demux_1_32_1_a7, demux_1_32_1_a8, demux_1_32_1_a9, demux_1_32_1_a10,
       demux_1_32_1_a11, demux_1_32_1_a16, demux_1_32_1_a17, demux_1_32_1_a18, demux_1_32_1_a19,
       demux_1_32_1_a24, demux_1_32_1_a25, demux_1_32_1_a26, demux_1_32_1_a27, multiplier_e_1_c0,
       multiplier_e_1_c1, multiplier_e_1_c2, multiplier_e_1_c3, multiplier_e_1_c4, multiplier_e_1_c5,
       multiplier_e_1_c6, multiplier_e_1_c7, multiplier_e_1_c8, multiplier_e_1_c9, multiplier_e_1_c10,
       multiplier_e_1_c11, multiplier_e_1_c12, multiplier_e_1_c13, multiplier_e_1_c14, multiplier_e_1_c15,
       not_1_c0, not_1_c1, not_1_c2, not_1_c3, not_1_c4, not_1_c5, not_1_c6, not_1_c7, or_2_out, or_3_out,
       or_4_out, or_5_c0, or_5_c1, or_5_c2, or_5_c3, or_5_c4, or_5_c5, or_5_c6, or_5_c7, sla_1_b0, sla_1_b1,
       sla_1_b2, sla_1_b3, sla_1_b4, sla_1_b5, sla_1_b6, sla_1_b7, sra_1_b0, sra_1_b1, sra_1_b2, sra_1_b3,
       sra_1_b4, sra_1_b5, sra_1_b6, sra_1_b7, subtractor_by_1_e_1_b0, subtractor_by_1_e_1_b1,
       subtractor_by_1_e_1_b2, subtractor_by_1_e_1_b3, subtractor_by_1_e_1_b4, subtractor_by_1_e_1_b5,
       subtractor_by_1_e_1_b6, subtractor_by_1_e_1_b7, subtractor_by_1_e_1_over_flow, subtractor_e_1_c0,
       subtractor_e_1_c1, subtractor_e_1_c2, subtractor_e_1_c3, subtractor_e_1_c4, subtractor_e_1_c5,
       subtractor_e_1_c6, subtractor_e_1_c7, subtractor_e_1_over_flow, xor_1_c0, xor_1_c1, xor_1_c2,
       xor_1_c3, xor_1_c4, xor_1_c5, xor_1_c6, xor_1_c7;

  DEMUX_1_32 demux_1_32_1 (
    .A0(demux_1_32_1_a0), .A1(demux_1_32_1_a1), .A2(demux_1_32_1_a2), .A3(demux_1_32_1_a3),
    .A4(demux_1_32_1_a4), .A5(demux_1_32_1_a5), .A6(demux_1_32_1_a6), .A7(demux_1_32_1_a7),
    .A8(demux_1_32_1_a8), .A9(demux_1_32_1_a9), .A10(demux_1_32_1_a10), .A11(demux_1_32_1_a11),
    .A16(demux_1_32_1_a16), .A17(demux_1_32_1_a17), .A18(demux_1_32_1_a18), .A19(demux_1_32_1_a19),
    .A24(demux_1_32_1_a24), .A25(demux_1_32_1_a25), .A26(demux_1_32_1_a26), .A27(demux_1_32_1_a27), .S4(S4),
    .S3(S3), .S2(S2), .S1(S1), .S0(S0), .E(E));  // open: A12, A13, A14, A15, A20, A21, A22, A23, A28, A29, A30, A31
  or or_1 (Over_Flow, subtractor_by_1_e_1_over_flow, subtractor_e_1_over_flow, adder_by_1_e_1_over_flow, adder_e_1_over_flow);
  Adder_E adder_e_1 (
    .E(demux_1_32_1_a0), .B7(B7), .A7(A7), .B6(B6), .A6(A6), .B5(B5), .A5(A5), .B4(B4), .A4(A4), .B3(B3),
    .A3(A3), .B2(B2), .A2(A2), .B1(B1), .A1(A1), .B0(B0), .A0(A0), .Over_Flow(adder_e_1_over_flow),
    .C7(adder_e_1_c7), .C6(adder_e_1_c6), .C5(adder_e_1_c5), .C4(adder_e_1_c4), .C3(adder_e_1_c3),
    .C2(adder_e_1_c2), .C1(adder_e_1_c1), .C0(adder_e_1_c0));
  or or_2 (or_2_out, demux_1_32_1_a4, demux_1_32_1_a5, demux_1_32_1_a6, demux_1_32_1_a7);
  or or_3 (or_3_out, demux_1_32_1_a8, demux_1_32_1_a9, demux_1_32_1_a10, demux_1_32_1_a11);
  or or_4 (or_4_out, demux_1_32_1_a24, demux_1_32_1_a25, demux_1_32_1_a26, demux_1_32_1_a27);
  Adder_by_1_E adder_by_1_e_1 (
    .E(demux_1_32_1_a1), .A7(A7), .A6(A6), .A5(A5), .A4(A4), .A3(A3), .A2(A2), .A1(A1), .A0(A0),
    .Over_Flow(adder_by_1_e_1_over_flow), .B7(adder_by_1_e_1_b7), .B6(adder_by_1_e_1_b6),
    .B5(adder_by_1_e_1_b5), .B4(adder_by_1_e_1_b4), .B3(adder_by_1_e_1_b3), .B2(adder_by_1_e_1_b2),
    .B1(adder_by_1_e_1_b1), .B0(adder_by_1_e_1_b0));
  Subtractor_E subtractor_e_1 (
    .E(demux_1_32_1_a2), .B7(B7), .A7(A7), .B6(B6), .A6(A6), .B5(B5), .A5(A5), .B4(B4), .A4(A4), .B3(B3),
    .A3(A3), .B2(B2), .A2(A2), .B1(B1), .A1(A1), .B0(B0), .A0(A0), .Over_Flow(subtractor_e_1_over_flow),
    .C7(subtractor_e_1_c7), .C6(subtractor_e_1_c6), .C5(subtractor_e_1_c5), .C4(subtractor_e_1_c4),
    .C3(subtractor_e_1_c3), .C2(subtractor_e_1_c2), .C1(subtractor_e_1_c1), .C0(subtractor_e_1_c0));
  Subtractor_by_1_E subtractor_by_1_e_1 (
    .E(demux_1_32_1_a3), .A7(A7), .A6(A6), .A5(A5), .A4(A4), .A3(A3), .A2(A2), .A1(A1), .A0(A0),
    .Over_Flow(subtractor_by_1_e_1_over_flow), .B7(subtractor_by_1_e_1_b7), .B6(subtractor_by_1_e_1_b6),
    .B5(subtractor_by_1_e_1_b5), .B4(subtractor_by_1_e_1_b4), .B3(subtractor_by_1_e_1_b3),
    .B2(subtractor_by_1_e_1_b2), .B1(subtractor_by_1_e_1_b1), .B0(subtractor_by_1_e_1_b0));
  Multiplier_E multiplier_e_1 (
    .E(or_2_out), .A7(B7), .A6(B6), .A5(B5), .A4(B4), .A3(B3), .A2(B2), .A1(B1), .A0(B0), .B7(A7), .B6(A6),
    .B5(A5), .B4(A4), .B3(A3), .B2(A2), .B1(A1), .B0(A0), .C15(multiplier_e_1_c15), .C14(multiplier_e_1_c14),
    .C13(multiplier_e_1_c13), .C12(multiplier_e_1_c12), .C11(multiplier_e_1_c11), .C10(multiplier_e_1_c10),
    .C9(multiplier_e_1_c9), .C8(multiplier_e_1_c8), .C7(multiplier_e_1_c7), .C6(multiplier_e_1_c6),
    .C5(multiplier_e_1_c5), .C4(multiplier_e_1_c4), .C3(multiplier_e_1_c3), .C2(multiplier_e_1_c2),
    .C1(multiplier_e_1_c1), .C0(multiplier_e_1_c0));
  And and_1 (
    .A0(A0), .A1(A1), .A2(A2), .A3(A3), .A4(A4), .A5(A5), .A6(A6), .A7(A7), .B0(B0), .B1(B1), .B2(B2),
    .B3(B3), .B4(B4), .B5(B5), .B6(B6), .B7(B7), .C0(and_1_c0), .C1(and_1_c1), .C2(and_1_c2), .C3(and_1_c3),
    .C4(and_1_c4), .C5(and_1_c5), .C6(and_1_c6), .C7(and_1_c7), .E(demux_1_32_1_a16));
  XOR xor_1 (
    .A0(A0), .A1(A1), .A2(A2), .A3(A3), .A4(A4), .A5(A5), .A6(A6), .A7(A7), .B0(B0), .B1(B1), .B2(B2),
    .B3(B3), .B4(B4), .B5(B5), .B6(B6), .B7(B7), .C0(xor_1_c0), .C1(xor_1_c1), .C2(xor_1_c2), .C3(xor_1_c3),
    .C4(xor_1_c4), .C5(xor_1_c5), .C6(xor_1_c6), .C7(xor_1_c7), .E(demux_1_32_1_a17));
  OR or_5 (
    .A0(A0), .A1(A1), .A2(A2), .A3(A3), .A4(A4), .A5(A5), .A6(A6), .A7(A7), .B0(B0), .B1(B1), .B2(B2),
    .B3(B3), .B4(B4), .B5(B5), .B6(B6), .B7(B7), .C0(or_5_c0), .C1(or_5_c1), .C2(or_5_c2), .C3(or_5_c3),
    .C4(or_5_c4), .C5(or_5_c5), .C6(or_5_c6), .C7(or_5_c7), .E(demux_1_32_1_a18));
  NOT not_1 (
    .A0(A0), .A1(A1), .A2(A2), .A3(A3), .A4(A4), .A5(A5), .A6(A6), .A7(A7), .C0(not_1_c0), .C1(not_1_c1),
    .C2(not_1_c2), .C3(not_1_c3), .C4(not_1_c4), .C5(not_1_c5), .C6(not_1_c6), .C7(not_1_c7),
    .E(demux_1_32_1_a19));
  SRA sra_1 (
    .A7(A7), .A6(A6), .A5(A5), .A4(A4), .A3(A3), .A2(A2), .A1(A1), .A0(A0), .B7(sra_1_b7), .B6(sra_1_b6),
    .B5(sra_1_b5), .B4(sra_1_b4), .B3(sra_1_b3), .B2(sra_1_b2), .B1(sra_1_b1), .B0(sra_1_b0), .E(or_3_out),
    .Rotate(Rotate_Shift));
  SLA sla_1 (
    .B7(sla_1_b7), .B6(sla_1_b6), .B5(sla_1_b5), .B4(sla_1_b4), .B3(sla_1_b3), .B2(sla_1_b2), .B1(sla_1_b1),
    .B0(sla_1_b0), .E(or_4_out), .Rotate(Rotate_Shift), .A7(A7), .A6(A6), .A5(A5), .A4(A4), .A3(A3), .A2(A2),
    .A1(A1), .A0(A0));
  or or_6 (C0, sla_1_b0, sra_1_b0, not_1_c0, or_5_c0, xor_1_c0, and_1_c0, multiplier_e_1_c0, subtractor_by_1_e_1_b0, subtractor_e_1_c0, adder_by_1_e_1_b0, adder_e_1_c0);
  or or_7 (C1, sla_1_b1, sra_1_b1, not_1_c1, or_5_c1, xor_1_c1, and_1_c1, multiplier_e_1_c1, subtractor_by_1_e_1_b1, subtractor_e_1_c1, adder_by_1_e_1_b1, adder_e_1_c1);
  or or_8 (C2, sla_1_b2, sra_1_b2, not_1_c2, or_5_c2, xor_1_c2, and_1_c2, multiplier_e_1_c2, subtractor_by_1_e_1_b2, subtractor_e_1_c2, adder_by_1_e_1_b2, adder_e_1_c2);
  or or_9 (C3, sla_1_b3, sra_1_b3, not_1_c3, or_5_c3, xor_1_c3, and_1_c3, multiplier_e_1_c3, subtractor_by_1_e_1_b3, subtractor_e_1_c3, adder_by_1_e_1_b3, adder_e_1_c3);
  or or_10 (C4, sla_1_b4, sra_1_b4, not_1_c4, or_5_c4, xor_1_c4, and_1_c4, multiplier_e_1_c4, subtractor_by_1_e_1_b4, subtractor_e_1_c4, adder_by_1_e_1_b4, adder_e_1_c4);
  or or_11 (C5, sla_1_b5, sra_1_b5, not_1_c5, or_5_c5, xor_1_c5, and_1_c5, multiplier_e_1_c5, subtractor_by_1_e_1_b5, subtractor_e_1_c5, adder_by_1_e_1_b5, adder_e_1_c5);
  or or_12 (C6, sla_1_b6, sra_1_b6, not_1_c6, or_5_c6, xor_1_c6, and_1_c6, multiplier_e_1_c6, subtractor_by_1_e_1_b6, subtractor_e_1_c6, adder_by_1_e_1_b6, adder_e_1_c6);
  or or_13 (C7, sla_1_b7, sra_1_b7, not_1_c7, or_5_c7, xor_1_c7, and_1_c7, multiplier_e_1_c7, subtractor_by_1_e_1_b7, subtractor_e_1_c7, adder_by_1_e_1_b7, adder_e_1_c7);
endmodule

module Micro_Adder (
  input  B7,
  input  B6,
  input  B5,
  input  B4,
  input  B3,
  input  B2,
  input  B1,
  input  B0,
  input  A7,
  input  A6,
  input  A5,
  input  A4,
  input  A3,
  input  A2,
  input  A1,
  input  A0,
  output Over_Flow,
  output C7,
  output C6,
  output C5,
  output C4,
  output C3,
  output C2,
  output C1,
  output C0
);

  Adder___Subtractor adder_subtractor_1 (
    .M(1'b0), .B7(B7), .A7(A7), .B6(B6), .A6(A6), .B5(B5), .A5(A5), .B4(B4), .A4(A4), .B3(B3), .A3(A3),
    .B2(B2), .A2(A2), .B1(B1), .A1(A1), .B0(B0), .A0(A0), .Over_Flow(Over_Flow), .C7(C7), .C6(C6), .C5(C5),
    .C4(C4), .C3(C3), .C2(C2), .C1(C1), .C0(C0));
endmodule

module Micro_Subtractor (
  input  B7,
  input  B6,
  input  B5,
  input  B4,
  input  B3,
  input  B2,
  input  B1,
  input  B0,
  input  A7,
  input  A6,
  input  A5,
  input  A4,
  input  A3,
  input  A2,
  input  A1,
  input  A0,
  output Over_Flow,
  output C7,
  output C6,
  output C5,
  output C4,
  output C3,
  output C2,
  output C1,
  output C0
);

  Adder___Subtractor adder_subtractor_1 (
    .M(1'b1), .B7(B7), .A7(A7), .B6(B6), .A6(A6), .B5(B5), .A5(A5), .B4(B4), .A4(A4), .B3(B3), .A3(A3),
    .B2(B2), .A2(A2), .B1(B1), .A1(A1), .B0(B0), .A0(A0), .Over_Flow(Over_Flow), .C7(C7), .C6(C6), .C5(C5),
    .C4(C4), .C3(C3), .C2(C2), .C1(C1), .C0(C0));
endmodule

module Micro_Multiplier (
  input  B7,
  input  B6,
  input  B5,
  input  B4,
  input  B3,
  input  B2,
  input  B1,
  input  B0,
  input  A7,
  input  A6,
  input  A5,
  input  A4,
  input  A3,
  input  A2,
  input  A1,
  input  A0,
  output C15,
  output C14,
  output C13,
  output C12,
  output C11,
  output C10,
  output C9,
  output C8,
  output C7,
  output C6,
  output C5,
  output C4,
  output C3,
  output C2,
  output C1,
  output C0
);

  Multiplier_8_Bit multiplier_8_bit_1 (
    .A0(B0), .A1(B1), .A2(B2), .A3(B3), .A4(B4), .A5(B5), .A6(B6), .A7(B7), .B7(A7), .B6(A6), .B5(A5),
    .B4(A4), .B3(A3), .B2(A2), .B1(A1), .B0(A0), .C15(C15), .C14(C14), .C13(C13), .C12(C12), .C11(C11),
    .C10(C10), .C9(C9), .C8(C8), .C7(C7), .C6(C6), .C5(C5), .C4(C4), .C3(C3), .C2(C2), .C1(C1), .C0(C0));
endmodule

module SRA (
  input  E,
  input  Rotate,
  input  A7,
  input  A6,
  input  A5,
  input  A4,
  input  A3,
  input  A2,
  input  A1,
  input  A0,
  output B7,
  output B6,
  output B5,
  output B4,
  output B3,
  output B2,
  output B1,
  output B0
);

  wire and_9_out;

  and and_1 (B7, E, and_9_out);
  and and_2 (B6, E, A7);
  and and_3 (B4, E, A5);
  and and_4 (B5, E, A6);
  and and_5 (B2, E, A3);
  and and_6 (B1, E, A2);
  and and_7 (B3, E, A4);
  and and_8 (B0, E, A1);
  and and_9 (and_9_out, Rotate, A0);
endmodule

module DEMUX_1_32 (
  input  E,
  input  S4,
  input  S3,
  input  S2,
  input  S1,
  input  S0,
  output A0,
  output A1,
  output A2,
  output A3,
  output A4,
  output A5,
  output A6,
  output A7,
  output A8,
  output A9,
  output A10,
  output A11,
  output A12,
  output A13,
  output A14,
  output A15,
  output A16,
  output A17,
  output A18,
  output A19,
  output A20,
  output A21,
  output A22,
  output A23,
  output A24,
  output A25,
  output A26,
  output A27,
  output A28,
  output A29,
  output A30,
  output A31
);

  wire not_1_out, not_2_out, not_3_out, not_4_out, not_5_out;

  not not_1 (not_1_out, S4);
  not not_2 (not_2_out, S3);
  not not_3 (not_3_out, S2);
  not not_4 (not_4_out, S0);
  not not_5 (not_5_out, S1);
  and _0 (A0, E, not_1_out, not_2_out, not_3_out, not_5_out, not_4_out);
  and _1 (A1, E, not_1_out, not_2_out, not_3_out, not_5_out, S0);
  and _2 (A2, E, not_1_out, not_2_out, not_3_out, S1, not_4_out);
  and _3 (A3, E, not_1_out, not_2_out, not_3_out, S1, S0);
  and _4 (A4, E, not_1_out, not_2_out, S2, not_5_out, not_4_out);
  and _5 (A5, E, not_1_out, not_2_out, S2, not_5_out, S0);
  and _6 (A6, E, not_1_out, not_2_out, S2, S1, not_4_out);
  and _7 (A7, E, not_1_out, not_2_out, S2, S1, S0);
  and _8 (A8, E, not_1_out, S3, not_3_out, not_5_out, not_4_out);
  and _9 (A9, E, not_1_out, S3, not_3_out, not_5_out, S0);
  and _10 (A10, E, not_1_out, S3, not_3_out, S1, not_4_out);
  and _11 (A11, E, not_1_out, S3, not_3_out, S1, S0);
  and _12 (A12, E, not_1_out, S3, S2, not_5_out, not_4_out);
  and _13 (A13, E, not_1_out, S3, S2, not_5_out, S0);
  and _14 (A14, E, not_1_out, S3, S2, S1, not_4_out);
  and _15 (A15, E, not_1_out, S3, S2, S1, S0);
  and _16 (A16, E, S4, not_2_out, not_3_out, not_5_out, not_4_out);
  and _17 (A17, E, S4, not_2_out, not_3_out, not_5_out, S0);
  and _18 (A18, E, S4, not_2_out, not_3_out, S1, not_4_out);
  and _19 (A19, E, S4, not_2_out, not_3_out, S1, S0);
  and _20 (A20, E, S4, not_2_out, S2, not_5_out, not_4_out);
  and _21 (A21, E, S4, not_2_out, S2, not_5_out, S0);
  and _22 (A22, E, S4, not_2_out, S2, S1, not_4_out);
  and _23 (A23, E, S4, not_2_out, S2, S1, S0);
  and _24 (A24, E, S4, S3, not_3_out, not_5_out, not_4_out);
  and _25 (A25, E, S4, S3, not_3_out, not_5_out, S0);
  and _26 (A26, E, S4, S3, not_3_out, S1, not_4_out);
  and _27 (A27, E, S4, S3, not_3_out, S1, S0);
  and _28 (A28, E, S4, S3, S2, not_5_out, not_4_out);
  and _29 (A29, E, S4, S3, S2, not_5_out, S0);
  and _30 (A30, E, S4, S3, S2, S1, not_4_out);
  and _31 (A31, E, S4, S3, S2, S1, S0);
endmodule

module Adder_E (
  input  B7,
  input  A7,
  input  B6,
  input  A6,
  input  B5,
  input  A5,
  input  B4,
  input  A4,
  input  B3,
  input  A3,
  input  B2,
  input  A2,
  input  B1,
  input  A1,
  input  B0,
  input  A0,
  input  E,
  output Over_Flow,
  output C7,
  output C6,
  output C5,
  output C4,
  output C3,
  output C2,
  output C1,
  output C0
);

  wire full_adder_1_cout, full_adder_1_s, full_adder_2_cout, full_adder_2_s, full_adder_3_cout,
       full_adder_3_s, full_adder_4_cout, full_adder_4_s, full_adder_5_cout, full_adder_5_s,
       full_adder_6_cout, full_adder_6_s, full_adder_7_cout, full_adder_7_s, full_adder_8_cout,
       full_adder_8_s, xor_1_out, xor_2_out, xor_3_out, xor_4_out, xor_5_out, xor_6_out, xor_7_out, xor_8_out;

  and and_1 (Over_Flow, E, full_adder_1_cout);
  xor xor_1 (xor_1_out, B7, 1'b0);
  Full_Adder full_adder_1 (
    .S(full_adder_1_s), .Cout(full_adder_1_cout), .A(A7), .B(xor_1_out), .Cin(full_adder_2_cout));
  and and_2 (C7, E, full_adder_1_s);
  xor xor_2 (xor_2_out, B5, 1'b0);
  xor xor_3 (xor_3_out, B6, 1'b0);
  Full_Adder full_adder_2 (
    .S(full_adder_2_s), .Cout(full_adder_2_cout), .A(A6), .B(xor_3_out), .Cin(full_adder_3_cout));
  and and_3 (C6, E, full_adder_2_s);
  and and_4 (C5, E, full_adder_3_s);
  xor xor_4 (xor_4_out, B4, 1'b0);
  Full_Adder full_adder_3 (
    .S(full_adder_3_s), .Cout(full_adder_3_cout), .A(A5), .B(xor_2_out), .Cin(full_adder_4_cout));
  Full_Adder full_adder_4 (
    .S(full_adder_4_s), .Cout(full_adder_4_cout), .A(A4), .B(xor_4_out), .Cin(full_adder_5_cout));
  and and_5 (C4, E, full_adder_4_s);
  xor xor_5 (xor_5_out, B3, 1'b0);
  Full_Adder full_adder_5 (
    .S(full_adder_5_s), .Cout(full_adder_5_cout), .A(A3), .B(xor_5_out), .Cin(full_adder_6_cout));
  and and_6 (C3, E, full_adder_5_s);
  xor xor_6 (xor_6_out, B2, 1'b0);
  Full_Adder full_adder_6 (
    .S(full_adder_6_s), .Cout(full_adder_6_cout), .A(A2), .B(xor_6_out), .Cin(full_adder_7_cout));
  and and_7 (C2, E, full_adder_6_s);
  xor xor_7 (xor_7_out, B1, 1'b0);
  Full_Adder full_adder_7 (
    .S(full_adder_7_s), .Cout(full_adder_7_cout), .A(A1), .B(xor_7_out), .Cin(full_adder_8_cout));
  and and_8 (C1, E, full_adder_7_s);
  xor xor_8 (xor_8_out, B0, 1'b0);
  Full_Adder full_adder_8 (.S(full_adder_8_s), .Cout(full_adder_8_cout), .A(A0), .B(xor_8_out), .Cin(1'b0));
  and and_9 (C0, E, full_adder_8_s);
endmodule

module Adder_by_1_E (
  input  A7,
  input  A6,
  input  A5,
  input  A4,
  input  A3,
  input  A2,
  input  A1,
  input  A0,
  input  E,
  output Over_Flow,
  output B7,
  output B6,
  output B5,
  output B4,
  output B3,
  output B2,
  output B1,
  output B0
);

  wire adder_subtractor_1_c0, adder_subtractor_1_c1, adder_subtractor_1_c2, adder_subtractor_1_c3,
       adder_subtractor_1_c4, adder_subtractor_1_c5, adder_subtractor_1_c6, adder_subtractor_1_c7,
       adder_subtractor_1_over_flow;

  and and_1 (Over_Flow, E, adder_subtractor_1_over_flow);
  and and_2 (B6, E, adder_subtractor_1_c6);
  and and_3 (B7, E, adder_subtractor_1_c7);
  and and_4 (B3, E, adder_subtractor_1_c3);
  and and_5 (B5, E, adder_subtractor_1_c5);
  and and_6 (B4, E, adder_subtractor_1_c4);
  and and_7 (B2, E, adder_subtractor_1_c2);
  and and_8 (B1, E, adder_subtractor_1_c1);
  and and_9 (B0, E, adder_subtractor_1_c0);
  Adder___Subtractor adder_subtractor_1 (
    .M(1'b0), .B7(1'b0), .A7(A7), .B6(1'b0), .A6(A6), .B5(1'b0), .A5(A5), .B4(1'b0), .A4(A4), .B3(1'b0),
    .A3(A3), .B2(1'b0), .A2(A2), .B1(1'b0), .A1(A1), .B0(1'b1), .A0(A0),
    .Over_Flow(adder_subtractor_1_over_flow), .C7(adder_subtractor_1_c7), .C6(adder_subtractor_1_c6),
    .C5(adder_subtractor_1_c5), .C4(adder_subtractor_1_c4), .C3(adder_subtractor_1_c3),
    .C2(adder_subtractor_1_c2), .C1(adder_subtractor_1_c1), .C0(adder_subtractor_1_c0));
endmodule

module Subtractor_by_1_E (
  input  A7,
  input  A6,
  input  A5,
  input  A4,
  input  A3,
  input  A2,
  input  A1,
  input  A0,
  input  E,
  output Over_Flow,
  output B7,
  output B6,
  output B5,
  output B4,
  output B3,
  output B2,
  output B1,
  output B0
);

  wire adder_subtractor_1_c0, adder_subtractor_1_c1, adder_subtractor_1_c2, adder_subtractor_1_c3,
       adder_subtractor_1_c4, adder_subtractor_1_c5, adder_subtractor_1_c6, adder_subtractor_1_c7,
       adder_subtractor_1_over_flow;

  and and_1 (Over_Flow, E, adder_subtractor_1_over_flow);
  and and_2 (B6, E, adder_subtractor_1_c6);
  and and_3 (B7, E, adder_subtractor_1_c7);
  and and_4 (B4, E, adder_subtractor_1_c4);
  and and_5 (B5, E, adder_subtractor_1_c5);
  and and_6 (B3, E, adder_subtractor_1_c3);
  and and_7 (B2, E, adder_subtractor_1_c2);
  and and_8 (B1, E, adder_subtractor_1_c1);
  and and_9 (B0, E, adder_subtractor_1_c0);
  Adder___Subtractor adder_subtractor_1 (
    .M(1'b1), .B7(1'b0), .A7(A7), .B6(1'b0), .A6(A6), .B5(1'b0), .A5(A5), .B4(1'b0), .A4(A4), .B3(1'b0),
    .A3(A3), .B2(1'b0), .A2(A2), .B1(1'b0), .A1(A1), .B0(1'b1), .A0(A0),
    .Over_Flow(adder_subtractor_1_over_flow), .C7(adder_subtractor_1_c7), .C6(adder_subtractor_1_c6),
    .C5(adder_subtractor_1_c5), .C4(adder_subtractor_1_c4), .C3(adder_subtractor_1_c3),
    .C2(adder_subtractor_1_c2), .C1(adder_subtractor_1_c1), .C0(adder_subtractor_1_c0));
endmodule

module Subtractor_E (
  input  B7,
  input  A7,
  input  B6,
  input  A6,
  input  B5,
  input  A5,
  input  B4,
  input  A4,
  input  B3,
  input  A3,
  input  B2,
  input  A2,
  input  B1,
  input  A1,
  input  B0,
  input  A0,
  input  E,
  output Over_Flow,
  output C7,
  output C6,
  output C5,
  output C4,
  output C3,
  output C2,
  output C1,
  output C0
);

  wire full_adder_1_cout, full_adder_1_s, full_adder_2_cout, full_adder_2_s, full_adder_3_cout,
       full_adder_3_s, full_adder_4_cout, full_adder_4_s, full_adder_5_cout, full_adder_5_s,
       full_adder_6_cout, full_adder_6_s, full_adder_7_cout, full_adder_7_s, full_adder_8_cout,
       full_adder_8_s, xor_1_out, xor_2_out, xor_3_out, xor_4_out, xor_5_out, xor_6_out, xor_7_out, xor_8_out;

  and and_1 (Over_Flow, E, full_adder_1_cout);
  xor xor_1 (xor_1_out, B7, 1'b1);
  Full_Adder full_adder_1 (
    .S(full_adder_1_s), .Cout(full_adder_1_cout), .A(A7), .B(xor_1_out), .Cin(full_adder_2_cout));
  and and_2 (C7, E, full_adder_1_s);
  xor xor_2 (xor_2_out, B6, 1'b1);
  xor xor_3 (xor_3_out, B5, 1'b1);
  Full_Adder full_adder_2 (
    .S(full_adder_2_s), .Cout(full_adder_2_cout), .A(A6), .B(xor_2_out), .Cin(full_adder_4_cout));
  and and_3 (C5, E, full_adder_4_s);
  and and_4 (C6, E, full_adder_2_s);
  xor xor_4 (xor_4_out, B4, 1'b1);
  Full_Adder full_adder_3 (
    .S(full_adder_3_s), .Cout(full_adder_3_cout), .A(A4), .B(xor_4_out), .Cin(full_adder_5_cout));
  Full_Adder full_adder_4 (
    .S(full_adder_4_s), .Cout(full_adder_4_cout), .A(A5), .B(xor_3_out), .Cin(full_adder_3_cout));
  and and_5 (C4, E, full_adder_3_s);
  xor xor_5 (xor_5_out, B3, 1'b1);
  Full_Adder full_adder_5 (
    .S(full_adder_5_s), .Cout(full_adder_5_cout), .A(A3), .B(xor_5_out), .Cin(full_adder_6_cout));
  and and_6 (C3, E, full_adder_5_s);
  xor xor_6 (xor_6_out, B2, 1'b1);
  Full_Adder full_adder_6 (
    .S(full_adder_6_s), .Cout(full_adder_6_cout), .A(A2), .B(xor_6_out), .Cin(full_adder_7_cout));
  and and_7 (C2, E, full_adder_6_s);
  xor xor_7 (xor_7_out, B1, 1'b1);
  Full_Adder full_adder_7 (
    .S(full_adder_7_s), .Cout(full_adder_7_cout), .A(A1), .B(xor_7_out), .Cin(full_adder_8_cout));
  and and_8 (C1, E, full_adder_7_s);
  xor xor_8 (xor_8_out, B0, 1'b1);
  Full_Adder full_adder_8 (.S(full_adder_8_s), .Cout(full_adder_8_cout), .A(A0), .B(xor_8_out), .Cin(1'b1));
  and and_9 (C0, E, full_adder_8_s);
endmodule

module Multiplier_E (
  input  A7,
  input  A6,
  input  A5,
  input  A4,
  input  A3,
  input  A2,
  input  A1,
  input  A0,
  input  B7,
  input  B6,
  input  B5,
  input  B4,
  input  B3,
  input  B2,
  input  B1,
  input  B0,
  input  E,
  output C15,
  output C14,
  output C13,
  output C12,
  output C11,
  output C10,
  output C9,
  output C8,
  output C7,
  output C6,
  output C5,
  output C4,
  output C3,
  output C2,
  output C1,
  output C0
);

  wire multiplier_8_bit_1_c0, multiplier_8_bit_1_c1, multiplier_8_bit_1_c2, multiplier_8_bit_1_c3,
       multiplier_8_bit_1_c4, multiplier_8_bit_1_c5, multiplier_8_bit_1_c6, multiplier_8_bit_1_c7,
       multiplier_8_bit_1_c8, multiplier_8_bit_1_c9, multiplier_8_bit_1_c10, multiplier_8_bit_1_c11,
       multiplier_8_bit_1_c12, multiplier_8_bit_1_c13, multiplier_8_bit_1_c14, multiplier_8_bit_1_c15;

  and and_1 (C14, E, multiplier_8_bit_1_c14);
  and and_2 (C13, E, multiplier_8_bit_1_c13);
  and and_3 (C15, E, multiplier_8_bit_1_c15);
  and and_4 (C12, E, multiplier_8_bit_1_c12);
  and and_5 (C11, E, multiplier_8_bit_1_c11);
  and and_6 (C10, E, multiplier_8_bit_1_c10);
  and and_7 (C9, E, multiplier_8_bit_1_c9);
  and and_8 (C8, E, multiplier_8_bit_1_c8);
  and and_9 (C7, E, multiplier_8_bit_1_c7);
  Multiplier_8_Bit multiplier_8_bit_1 (
    .A0(A0), .A1(A1), .A2(A2), .A3(A3), .A4(A4), .A5(A5), .A6(A6), .A7(A7), .B7(B7), .B6(B6), .B5(B5),
    .B4(B4), .B3(B3), .B2(B2), .B1(B1), .B0(B0), .C15(multiplier_8_bit_1_c15), .C14(multiplier_8_bit_1_c14),
    .C13(multiplier_8_bit_1_c13), .C12(multiplier_8_bit_1_c12), .C11(multiplier_8_bit_1_c11),
    .C10(multiplier_8_bit_1_c10), .C9(multiplier_8_bit_1_c9), .C8(multiplier_8_bit_1_c8),
    .C7(multiplier_8_bit_1_c7), .C6(multiplier_8_bit_1_c6), .C5(multiplier_8_bit_1_c5),
    .C4(multiplier_8_bit_1_c4), .C3(multiplier_8_bit_1_c3), .C2(multiplier_8_bit_1_c2),
    .C1(multiplier_8_bit_1_c1), .C0(multiplier_8_bit_1_c0));
  and and_10 (C5, E, multiplier_8_bit_1_c5);
  and and_11 (C6, E, multiplier_8_bit_1_c6);
  and and_12 (C4, E, multiplier_8_bit_1_c4);
  and and_13 (C3, E, multiplier_8_bit_1_c3);
  and and_14 (C1, E, multiplier_8_bit_1_c1);
  and and_15 (C0, E, multiplier_8_bit_1_c0);
  and and_16 (C2, E, multiplier_8_bit_1_c2);
endmodule
