// Logisim project MUX 32-1.circ as structural Verilog: 1 circuit, main circuit main
module main (
  input  _0,
  input  _1,
  input  _2,
  input  _3,
  input  _4,
  input  _5,
  input  _6,
  input  _7,
  input  _8,
  input  _9,
  input  _10,
  input  _11,
  input  _12,
  input  _13,
  input  _14,
  input  _15,
  input  _16,
  input  _17,
  input  _18,
  input  _19,
  input  _20,
  input  _21,
  input  _22,
  input  _23,
  input  _24,
  input  _25,
  input  _26,
  input  _27,
  input  _28,
  input  _29,
  input  _30,
  input  _31,
  input  S0,
  input  S1,
  input  S2,
  input  S3,
  input  S4
);

  wire and_1_out, and_2_out, and_3_out, and_4_out, and_5_out, and_6_out, and_7_out, and_8_out, and_9_out,
       and_10_out, and_11_out, and_12_out, and_13_out, and_14_out, and_15_out, and_16_out, and_17_out,
       and_18_out, and_19_out, and_20_out, and_21_out, and_22_out, and_23_out, and_24_out, and_25_out,
       and_26_out, and_27_out, and_28_out, and_29_out, and_30_out, and_31_out, and_32_out, not_1_out,
       not_2_out, not_3_out, not_4_out, not_5_out, or_1_out, or_2_out, or_3_out, or_4_out, or_5_out,
       or_6_out, or_7_out, or_8_out, or_9_out, or_10_out;

  not not_1 (not_1_out, S4);
  not not_2 (not_2_out, S3);
  not not_3 (not_3_out, S1);
  not not_4 (not_4_out, S2);
  not not_5 (not_5_out, S0);
  and and_1 (and_1_out, not_5_out, not_3_out, not_4_out, not_2_out, not_1_out, _0);
  and and_2 (and_2_out, S0, not_3_out, not_4_out, not_2_out, not_1_out, _1);
  and and_3 (and_3_out, not_5_out, S1, not_4_out, not_2_out, not_1_out, _2);
  and and_4 (and_4_out, S0, S1, not_4_out, not_2_out, not_1_out, _3);
  and and_5 (and_5_out, not_5_out, not_3_out, S2, not_2_out, not_1_out, _4);
  and and_6 (and_6_out, S0, not_3_out, S2, not_2_out, not_1_out, _5);
  and and_7 (and_7_out, not_5_out, S1, S2, not_2_out, not_1_out, _6);
  and and_8 (and_8_out, S0, S1, S2, not_2_out, not_1_out, _7);
  and and_9 (and_9_out, not_5_out, not_3_out, not_4_out, S3, not_1_out, _8);
  and and_10 (and_10_out, S0, not_3_out, not_4_out, S3, not_1_out, _9);
  and and_11 (and_11_out, not_5_out, S1, not_4_out, S3, not_1_out, _10);
  and and_12 (and_12_out, S0, S1, not_4_out, S3, not_1_out, _11);
  and and_13 (and_13_out, not_5_out, not_3_out, S2, S3, not_1_out, _12);
  and and_14 (and_14_out, S0, not_3_out, S2, S3, not_1_out, _13);
  and and_15 (and_15_out, not_5_out, S1, S2, S3, not_1_out, _14);
  and and_16 (and_16_out, S0, S1, S2, S3, not_1_out, _15);
  and and_17 (and_17_out, not_5_out, not_3_out, not_4_out, not_2_out, S4, _16);
  and and_18 (and_18_out, S0, not_3_out, not_4_out, not_2_out, S4, _17);
  and and_19 (and_19_out, not_5_out, S1, not_4_out, not_2_out, S4, _18);
  and and_20 (and_20_out, S0, S1, not_4_out, not_2_out, S4, _19);
  and and_21 (and_21_out, not_5_out, not_3_out, S2, not_2_out, S4, _20);
  and and_22 (and_22_out, S0, not_3_out, S2, not_2_out, S4, _21);
  and and_23 (and_23_out, not_5_out, S1, S2, not_2_out, S4, _22);
  and and_24 (and_24_out, S0, S1, S2, not_2_out, S4, _23);
  and and_25 (and_25_out, not_5_out, not_3_out, not_4_out, S3, S4, _24);
  and and_26 (and_26_out, S0, not_3_out, not_4_out, S3, S4, _25);
  and and_27 (and_27_out, not_5_out, S1, not_4_out, S3, S4, _26);
  and and_28 (and_28_out, S0, S1, not_4_out, S3, S4, _27);
  and and_29 (and_29_out, not_5_out, not_3_out, S2, S3, S4, _28);
  and and_30 (and_30_out, S0, not_3_out, S2, S3, S4, _29);
  and and_31 (and_31_out, not_5_out, S1, S2, S3, S4, _30);
  and and_32 (and_32_out, S0, S1, S2, S3, S4, _31);
  or or_1 (or_1_out, and_1_out, and_2_out, and_3_out, and_4_out);
  or or_2 (or_2_out, and_5_out, and_6_out, and_7_out, and_8_out);
  or or_3 (or_3_out, and_9_out, and_10_out, and_11_out, and_12_out);
  or or_4 (or_4_out, and_13_out, and_14_out, and_15_out, and_16_out);
  or or_5 (or_5_out, and_17_out, and_18_out, and_19_out, and_20_out);
  or or_6 (or_6_out, and_21_out, and_22_out, and_23_out, and_24_out);
  or or_7 (or_7_out, and_25_out, and_26_out, and_27_out, and_28_out);
  or or_8 (or_8_out, and_29_out, and_30_out, and_31_out, and_32_out);
  or or_9 (or_9_out, or_1_out, or_2_out, or_3_out, or_4_out);
  or or_10 (or_10_out, or_5_out, or_6_out, or_7_out, or_8_out);
  // OR_Gate or_11 has open pins: in0=or_9_out, in1=or_10_out, out=open
endmodule
