// Logisim project MUX 8-1.circ as structural Verilog: 1 circuit, main circuit MUX 8-1
module MUX_8_1 (
  input  A0,
  input  A1,
  input  A2,
  input  A3,
  input  A4,
  input  A5,
  input  A6,
  input  A7,
  input  S0,
  input  S1,
  input  S2,
  output out_12
);

  wire and_1_out, and_2_out, and_3_out, and_4_out, and_5_out, and_6_out, and_7_out, and_8_out, not_1_out,
       not_2_out, not_3_out, or_1_out, or_2_out;

  not not_1 (not_1_out, S1);
  not not_2 (not_2_out, S2);
  not not_3 (not_3_out, S0);
  and and_1 (and_1_out, not_3_out, not_1_out, not_2_out, A0);
  and and_2 (and_2_out, S0, not_1_out, not_2_out, A1);
  and and_3 (and_3_out, not_3_out, S1, not_2_out, A2);
  and and_4 (and_4_out, S0, S1, not_2_out, A3);
  and and_5 (and_5_out, not_3_out, not_1_out, S2, A4);
  and and_6 (and_6_out, S0, not_1_out, S2, A5);
  and and_7 (and_7_out, not_3_out, S1, S2, A6);
  and and_8 (and_8_out, S0, S1, S2, A7);
  or or_1 (or_1_out, and_1_out, and_2_out, and_3_out, and_4_out);
  or or_2 (or_2_out, and_5_out, and_6_out, and_7_out, and_8_out);
  or or_3 (out_12, or_1_out, or_2_out);
endmodule
